// Logisim project MIPSarhitektura.circ as structural Verilog: 48 circuits, main circuit main
module main (
);

  wire alucontrol_1_sv, and_2_out, and_3_out, and_4_out, Branch, CLK, Exception, exmemreg_1_memtoregmem,
       exmemreg_1_memwritemem, EXRegWrite, IDBranch, idexreg_1_alusrcex, idexreg_1_linkex,
       idexreg_1_memtoregex, idexreg_1_memwriteex, idexreg_1_regdstex, IFIDWrite, InvalidInstr,
       jedinicazadetekcijuhazarda_1_ifidwrite, jedinicazadetekcijuhazarda_1_pcwrite, JR, JumpCtrl, LinkB,
       LinkJ, LinkRa, LinkRegEX, LinkRegID, MC, MEMMemRead, MEMReadEX, MEMRegWrite,
       memsizecheck_1_invalidadress, MemToRegCtrl, MemToRegID, memwbreg_1_memtoregwb, MTC, not_1_out,
       not_2_out, not_3_out, not_4_out, not_5_out, not_6_out, novialu32bit_1_overflow, novicontrol_1_alusrc,
       novicontrol_1_memread, novicontrol_1_memwrite, novicontrol_1_regdst, or_1_out, or_2_out, or_4_out,
       PCWrite, RegWriteCtrl, RegWriteID, RegWS, RST, Stall;
  wire [1:0] FwA, FwB, FwBr1, FwBr2, idexreg_1_aluopex, novicontrol_1_aluop, novicontrol_1_storecontrol, SOE,
       SOM;
  wire [2:0] LOE, LOM, novicontrol_1_loadcontrol;
  wire [3:0] alucontrol_1_alucontrol, storecontrol_1_le;
  wire [4:0] IFIDRs, IFIDRt, multiplexer_7_out, RdEX, RdMEM, RsEX, RtEX, SaEX, WR, WriteReg;
  wire [5:0] IDInstr, Op, OpEx;
  wire [7:0] undriven, undriven_2, undriven_3, undriven_4;
  wire [15:6] ifidreg_1_instrukcijaid;
  wire [31:0] A, add32bit_1_out_3, ALUrez, ALUrezWB, B, Badress, epccause_1_causeizlaz, epccause_1_epcizlaz,
       EPCCS, exceptioncontrol_1_cause, exmemreg_1_readdata2mem, IDA1B, IDB1B, idexreg_1_pcplus4ex,
       idexreg_1_signextex, instrukcijskamemorija_1_out_2, memwbreg_1_readdatawb, multiplexer_1_out,
       multiplexer_2_out, multiplexer_3_out, multiplexer_4_out, multiplexer_9_out, multiplexer_11_out,
       multiplexer_14_out, multiplexer_15_out, novialu32bit_1_aluresult, pc_1_izlaz, PCplus4ID, ReadData1EX,
       ReadData1ID, ReadData2EX, ReadData2ID, ReadDataMem, registarskadatoteka_1_r8, sll32bit_1_izlaz,
       storecontrol_1_do, WriteData;

  // Probe on Badress
  Multiplexer #(.width(32)) multiplexer_1 (
    .in0(add32bit_1_out_3), .in1(Badress), .out(multiplexer_1_out), .sel(Branch));
  Multiplexer #(.width(32)) multiplexer_2 (
    .in0(multiplexer_1_out), .in1(multiplexer_4_out), .out(multiplexer_2_out), .sel(JumpCtrl));
  Multiplexer #(.width(32)) multiplexer_3 (
    .in0(multiplexer_2_out), .in1(32'h10010180), .out(multiplexer_3_out), .sel(Exception));
  Button button_1 (.out(RST));
  // Probe on pc_1_izlaz
  PC pc_1 (.Ulaz(multiplexer_3_out), .PCWrite(PCWrite), .CLK(CLK), .RST(RST), .Izlaz(pc_1_izlaz));
  Multiplexer #(.width(32)) multiplexer_4 (
    .in0({PCplus4ID[31:28], IFIDRs, IFIDRt, ifidreg_1_instrukcijaid, IDInstr, 2'b00}), .in1(IDA1B),
    .out(multiplexer_4_out), .sel(JR));
  ADD32bit add32bit_1 (.in_1(32'h4), .in_2(pc_1_izlaz), .out_3(add32bit_1_out_3));  // open: out_4
  or or_1 (or_1_out, Exception, JumpCtrl, Branch);
  InstrukcijskaMemorija instrukcijskamemorija_1 (.in_1(pc_1_izlaz), .out_2(instrukcijskamemorija_1_out_2));
  // Probe on instrukcijskamemorija_1_out_2
  Clock clock_1 (.out(CLK));
  IFIDReg ifidreg_1 (
    .PCplus4IF(add32bit_1_out_3), .InstrukcijaIF(instrukcijskamemorija_1_out_2), .Flush(or_1_out),
    .IFIDWrite(IFIDWrite), .CLK(CLK), .RST(RST), .PCplus4ID(PCplus4ID),
    .InstrukcijaID({Op, IFIDRs, IFIDRt, ifidreg_1_instrukcijaid, IDInstr}));
  // Probe on {Op, IFIDRs, IFIDRt, ifidreg_1_instrukcijaid, IDInstr}
  Multiplexer #(.select(2), .width(32)) multiplexer_5 (
    .in0(ReadData1ID), .in1(ALUrez), .in2(WriteData), .out(IDA1B), .sel(FwBr1));  // open: in3
  not not_1 (not_1_out, CLK);
  JedinicaZaDetekcijuHazarda jedinicazadetekcijuhazarda_1 (
    .IFIDRs(IFIDRs), .IFIDRt(IFIDRt), .MemReadEx(MEMReadEX), .EXWriteReg(WR), .IDBranch(IDBranch),
    .EXRegWrite(EXRegWrite), .MEMMemRead(MEMMemRead), .MEMWriteReg(RdMEM), .JumpReg(JR),
    .PCWrite(jedinicazadetekcijuhazarda_1_pcwrite), .IFIDWrite(jedinicazadetekcijuhazarda_1_ifidwrite),
    .MuxControl(Stall));
  noviControl novicontrol_1 (
    .Ulaz(Op), .RegDst(novicontrol_1_regdst), .Branch(IDBranch), .MemRead(novicontrol_1_memread),
    .MemToReg(MemToRegCtrl), .ALUOp(novicontrol_1_aluop), .MemWrite(novicontrol_1_memwrite),
    .ALUSrc(novicontrol_1_alusrc), .RegWrite(RegWriteCtrl), .StoreControl(novicontrol_1_storecontrol),
    .LoadControl(novicontrol_1_loadcontrol));  // open: Jump
  // Probe on registarskadatoteka_1_r8
  // Probe on ReadData2ID
  not not_2 (not_2_out, LinkB);
  not not_3 (not_3_out, LinkJ);
  RegistarskaDatoteka registarskadatoteka_1 (
    .RegWrite(RegWS), .WriteData(WriteData), .WriteReg(WriteReg), .ReadReg1(IFIDRs), .ReadReg2(IFIDRt),
    .CLK(not_1_out), .RST(RST), .ReadData1(ReadData1ID), .ReadData2(ReadData2ID),
    .R8(registarskadatoteka_1_r8));
  SLL32bit sll32bit_1 (
    .Ulaz({{17{ifidreg_1_instrukcijaid[15]}}, ifidreg_1_instrukcijaid[14:6], IDInstr}), .Ctrl(5'b00010),
    .Izlaz(sll32bit_1_izlaz));
  and and_1 (MemToRegID, MemToRegCtrl, not_2_out, not_3_out);
  Multiplexer #(.select(2), .width(32)) multiplexer_6 (
    .in0(ReadData2ID), .in1(ALUrez), .in2(WriteData), .out(IDB1B), .sel(FwBr2));  // open: in3
  JedinicaZaDetekcijuGrananja jedinicazadetekcijugrananja_1 (
    .ReadData1(IDA1B), .ReadData2(IDB1B), .Opcode(Op), .ReadReg2(IFIDRt), .Branch(Branch), .Link(LinkB));
  or or_2 (or_2_out, Exception, Stall);
  ADD32bit add32bit_2 (.in_1(sll32bit_1_izlaz), .in_2(PCplus4ID), .out_3(Badress));  // open: out_4
  ZadrskaJDH zadrskajdh_1 (
    .PCWriteI(jedinicazadetekcijuhazarda_1_pcwrite), .IFIDWriteI(jedinicazadetekcijuhazarda_1_ifidwrite),
    .CLK(CLK), .RST(RST), .PCWrite(PCWrite), .IFIDWrite(IFIDWrite));
  // Probe on novicontrol_1_aluop
  or or_3 (RegWriteID, RegWriteCtrl, LinkB, LinkJ);
  IDEXReg idexreg_1 (
    .PCplus4ID(PCplus4ID), .ReadData1ID(ReadData1ID), .ReadData2ID(ReadData2ID),
    .SignExtID({{17{ifidreg_1_instrukcijaid[15]}}, ifidreg_1_instrukcijaid[14:6], IDInstr}),
    .RegDstID(novicontrol_1_regdst), .AluOpID(novicontrol_1_aluop), .AluSrcID(novicontrol_1_alusrc),
    .LinkID(LinkRa), .MemWriteID(novicontrol_1_memwrite), .MemReadID(novicontrol_1_memread),
    .RegWriteID(RegWriteID), .MemToRegID(MemToRegID), .ID25do21(IFIDRs), .ID20do16(IFIDRt),
    .ID15do11(ifidreg_1_instrukcijaid[15:11]), .StoreOpID(novicontrol_1_storecontrol),
    .LoadOpID(novicontrol_1_loadcontrol), .OpID(Op), .SaID(ifidreg_1_instrukcijaid[10:6]),
    .LinkRegID(LinkRegID), .Flush(or_2_out), .CLK(CLK), .RST(RST), .PCplus4EX(idexreg_1_pcplus4ex),
    .ReadData1EX(ReadData1EX), .ReadData2EX(ReadData2EX), .SignExtEX(idexreg_1_signextex),
    .RegDstEX(idexreg_1_regdstex), .AluOpEX(idexreg_1_aluopex), .AluSrcEX(idexreg_1_alusrcex),
    .LinkEX(idexreg_1_linkex), .MemWriteEX(idexreg_1_memwriteex), .MemReadEX(MEMReadEX),
    .RegWriteEX(EXRegWrite), .MemToRegEX(idexreg_1_memtoregex), .EX25do21({RsEX[4:3], MTC, RsEX[1:0]}),
    .EX20do16(RtEX), .EX15do11(RdEX), .StoreOpEx(SOE), .LoadOpEx(LOE), .OpEX(OpEx), .SaEX(SaEX),
    .LinkRegEX(LinkRegEX));
  // Probe on idexreg_1_signextex
  Multiplexer #(.width(5)) multiplexer_7 (.in0(RtEX), .in1(RdEX), .out(multiplexer_7_out), .sel(idexreg_1_regdstex));
  JedinicaZaDetekcijuSkokova jedinicazadetekcijuskokova_1 (
    .Op(Op), .Instr(IDInstr), .Jump(JumpCtrl), .JR(JR), .Link(LinkJ), .LinkReg(LinkRegID));
  and and_2 (and_2_out, MTC, MC);
  and and_3 (and_3_out, idexreg_1_linkex, not_4_out);
  Multiplexer #(.width(5)) multiplexer_8 (.in0(multiplexer_7_out), .in1({5{1'b1}}), .out(WR), .sel(and_3_out));
  or or_4 (or_4_out, and_2_out, Exception);
  not not_4 (not_4_out, LinkRegEX);
  Multiplexer #(.width(32)) multiplexer_9 (
    .in0(exceptioncontrol_1_cause), .in1(ReadData2EX), .out(multiplexer_9_out), .sel(MTC));
  or or_5 (LinkRa, LinkJ, LinkB);
  Multiplexer #(.select(2), .width(32)) multiplexer_10 (
    .in0(ReadData1EX), .in1(ALUrez), .in2(WriteData), .out(A), .sel(FwA));  // open: in3
  not not_5 (not_5_out, MTC);
  Multiplexer #(.width(32)) multiplexer_11 (
    .in0(B), .in1(idexreg_1_signextex), .out(multiplexer_11_out), .sel(idexreg_1_alusrcex));
  ALUControl alucontrol_1 (
    .ALUOp(idexreg_1_aluopex), .Instr(idexreg_1_signextex[5:0]), .Op(OpEx),
    .ALUControl(alucontrol_1_alucontrol), .SV(alucontrol_1_sv), .Invalid(InvalidInstr));
  EpcCause epccause_1 (
    .CauseReg(multiplexer_9_out), .AdresaInstrukcije(idexreg_1_pcplus4ex), .Izuzetak(or_4_out), .CLK(CLK),
    .RST(RST), .CauseIzlaz(epccause_1_causeizlaz), .EpcIzlaz(epccause_1_epcizlaz));
  Multiplexer #(.width(32)) multiplexer_12 (
    .in0(epccause_1_causeizlaz), .in1(epccause_1_epcizlaz), .out(EPCCS), .sel(RdEX[0]));
  and and_4 (and_4_out, not_5_out, MC);
  Multiplexer #(.width(32)) multiplexer_13 (.in0(multiplexer_14_out), .in1(EPCCS), .out(B), .sel(and_4_out));
  Multiplexer #(.select(2), .width(32)) multiplexer_14 (
    .in0(ReadData2EX), .in1(ALUrez), .in2(WriteData), .out(multiplexer_14_out), .sel(FwB));  // open: in3
  not not_6 (not_6_out, OpEx[4]);
  noviALU32bit novialu32bit_1 (
    .A(A), .B(multiplexer_11_out), .ALUControl(alucontrol_1_alucontrol), .Sa(SaEX), .SV(alucontrol_1_sv),
    .ALUresult(novialu32bit_1_aluresult), .Overflow(novialu32bit_1_overflow));  // open: ZeroFlag
  JedinicaZaProsljedjivanje jedinicazaprosljedjivanje_1 (
    .MEMRegWrite(MEMRegWrite), .WBRegWrite(RegWS), .RdMEM(RdMEM), .Rs({RsEX[4:3], MTC, RsEX[1:0]}),
    .RdWB(WriteReg), .Rt(RtEX), .RsID(IFIDRs), .RtID(IFIDRt), .ForwardA(FwA), .ForwardB(FwB),
    .ForwardBranch1(FwBr1), .ForwardBranch2(FwBr2));
  nor nor_1 (MC, OpEx[0], OpEx[1], OpEx[2], OpEx[3], not_6_out, OpEx[5]);
  Multiplexer #(.width(32)) multiplexer_15 (
    .in0(novialu32bit_1_aluresult), .in1(idexreg_1_pcplus4ex), .out(multiplexer_15_out),
    .sel(idexreg_1_linkex));
  Clock clock_2 (.out(CLK));
  ExceptionControl exceptioncontrol_1 (
    .Overflow(novialu32bit_1_overflow), .InvalidAdress(memsizecheck_1_invalidadress),
    .InvalidInsruction(InvalidInstr), .Exception(Exception), .Cause(exceptioncontrol_1_cause));
  MemSizeCheck memsizecheck_1 (
    .Adress(multiplexer_15_out), .MemRead(MEMReadEX), .MemWrite(idexreg_1_memwriteex),
    .Rs({RsEX[4:3], MTC, RsEX[1:0]}), .InvalidAdress(memsizecheck_1_invalidadress));
  EXMEMReg exmemreg_1 (
    .ALUrezEX(multiplexer_15_out), .ReadData2EX(B), .WriteRegisterEX(WR), .RegWriteEX(EXRegWrite),
    .MemToRegEX(idexreg_1_memtoregex), .MemReadEX(MEMReadEX), .MemWriteEX(idexreg_1_memwriteex),
    .StoreOpEx(SOE), .LoadOpEx(LOE), .Flush(Exception), .CLK(CLK), .RST(RST), .ALUrezMEM(ALUrez),
    .ReadData2MEM(exmemreg_1_readdata2mem), .WriteRegisterMEM(RdMEM), .RegWriteMEM(MEMRegWrite),
    .MemToRegMEM(exmemreg_1_memtoregmem), .MemReadMEM(MEMMemRead), .MemWriteMEM(exmemreg_1_memwritemem),
    .StoreOpMem(SOM), .LoadOpMem(LOM));
  // Probe on exmemreg_1_readdata2mem
  StoreControl storecontrol_1 (
    .StoreOp(SOM), .DI(exmemreg_1_readdata2mem), .LE(storecontrol_1_le), .DO(storecontrol_1_do));
  // Probe on ALUrez
  // RAM #(.addrWidth(24), .enables("line"), .line("quad"), .misaligned("true")) ram_1: pin names not known; wires that end beside it: ALUrez[23:0], exmemreg_1_memwritemem, storecontrol_1_le[0], storecontrol_1_le[1], storecontrol_1_le[2], storecontrol_1_le[3], CLK, storecontrol_1_do[31:24], storecontrol_1_do[23:16], storecontrol_1_do[15:8], storecontrol_1_do[7:0]
  LoadControl loadcontrol_1 (
    .OE(MEMMemRead), .LoadOp(LOM), .DI({undriven_4, undriven_3, undriven_2, undriven}), .DO(ReadDataMem));
  MEMWBReg memwbreg_1 (
    .ALUrezMEM(ALUrez), .ReadDataMEM(ReadDataMem), .RegWriteMEM(MEMRegWrite),
    .MemToRegMEM(exmemreg_1_memtoregmem), .OdredisnaAdresaMEM(RdMEM), .CLK(CLK), .RST(RST),
    .ALUrezWB(ALUrezWB), .ReadDataWB(memwbreg_1_readdatawb), .RegWriteWB(RegWS),
    .MemToRegWB(memwbreg_1_memtoregwb), .OdredisnaAdresaWB(WriteReg));
  Multiplexer #(.width(32)) multiplexer_16 (
    .in0(ALUrezWB), .in1(memwbreg_1_readdatawb), .out(WriteData), .sel(memwbreg_1_memtoregwb));

  // Other names for the same wires on the sheet: RsEX[2] = MTC
endmodule

module RegistarskaDatoteka (
  input  RegWrite,
  input  [31:0] WriteData,
  input  [4:0] WriteReg,
  input  [4:0] ReadReg1,
  input  [4:0] ReadReg2,
  input  CLK,
  input  RST,
  output [31:0] ReadData1,
  output [31:0] ReadData2,
  output [31:0] R8
);

  wire demultiplexer_1_out1, demultiplexer_1_out2, demultiplexer_1_out3, demultiplexer_1_out4,
       demultiplexer_1_out5, demultiplexer_1_out6, demultiplexer_1_out7, demultiplexer_1_out8,
       demultiplexer_1_out9, demultiplexer_1_out10, demultiplexer_1_out11, demultiplexer_1_out12,
       demultiplexer_1_out13, demultiplexer_1_out14, demultiplexer_1_out15, demultiplexer_1_out16,
       demultiplexer_1_out17, demultiplexer_1_out18, demultiplexer_1_out19, demultiplexer_1_out20,
       demultiplexer_1_out21, demultiplexer_1_out22, demultiplexer_1_out23, demultiplexer_1_out24,
       demultiplexer_1_out25, demultiplexer_1_out26, demultiplexer_1_out27, demultiplexer_1_out28,
       demultiplexer_1_out29, demultiplexer_1_out30, demultiplexer_1_out31, RW;
  wire [31:0] r1, r2, r3, r4, r5, r6, r7, r9, r10, r11, r12, r13, r14, r15, r16, r17, r18, r19, r20, r21,
       r22, r23, r24, r25, r26, r27, r28, r29, r30, r31;

  and and_1 (RW, RegWrite, CLK);
  Demultiplexer #(.select(5)) demultiplexer_1 (
    .out1(demultiplexer_1_out1), .out2(demultiplexer_1_out2), .out3(demultiplexer_1_out3),
    .out4(demultiplexer_1_out4), .out5(demultiplexer_1_out5), .out6(demultiplexer_1_out6),
    .out7(demultiplexer_1_out7), .out8(demultiplexer_1_out8), .out9(demultiplexer_1_out9),
    .out10(demultiplexer_1_out10), .out11(demultiplexer_1_out11), .out12(demultiplexer_1_out12),
    .out13(demultiplexer_1_out13), .out14(demultiplexer_1_out14), .out15(demultiplexer_1_out15),
    .out16(demultiplexer_1_out16), .out17(demultiplexer_1_out17), .out18(demultiplexer_1_out18),
    .out19(demultiplexer_1_out19), .out20(demultiplexer_1_out20), .out21(demultiplexer_1_out21),
    .out22(demultiplexer_1_out22), .out23(demultiplexer_1_out23), .out24(demultiplexer_1_out24),
    .out25(demultiplexer_1_out25), .out26(demultiplexer_1_out26), .out27(demultiplexer_1_out27),
    .out28(demultiplexer_1_out28), .out29(demultiplexer_1_out29), .out30(demultiplexer_1_out30),
    .out31(demultiplexer_1_out31), .in(RW), .sel(WriteReg));  // open: out0
  Registar32bit registar32bit_1 (.Ulaz(WriteData), .CLK(demultiplexer_1_out1), .RST(RST), .Izlaz(r1));
  Registar32bit registar32bit_2 (.Ulaz(WriteData), .CLK(demultiplexer_1_out2), .RST(RST), .Izlaz(r2));
  Registar32bit registar32bit_3 (.Ulaz(WriteData), .CLK(demultiplexer_1_out3), .RST(RST), .Izlaz(r3));
  Registar32bit registar32bit_4 (.Ulaz(WriteData), .CLK(demultiplexer_1_out4), .RST(RST), .Izlaz(r4));
  Registar32bit registar32bit_5 (.Ulaz(WriteData), .CLK(demultiplexer_1_out5), .RST(RST), .Izlaz(r5));
  Registar32bit registar32bit_6 (.Ulaz(WriteData), .CLK(demultiplexer_1_out6), .RST(RST), .Izlaz(r6));
  Registar32bit registar32bit_7 (.Ulaz(WriteData), .CLK(demultiplexer_1_out7), .RST(RST), .Izlaz(r7));
  Registar32bit registar32bit_8 (.Ulaz(WriteData), .CLK(demultiplexer_1_out8), .RST(RST), .Izlaz(R8));
  Registar32bit registar32bit_9 (.Ulaz(WriteData), .CLK(demultiplexer_1_out9), .RST(RST), .Izlaz(r9));
  Registar32bit registar32bit_10 (.Ulaz(WriteData), .CLK(demultiplexer_1_out10), .RST(RST), .Izlaz(r10));
  Registar32bit registar32bit_11 (.Ulaz(WriteData), .CLK(demultiplexer_1_out11), .RST(RST), .Izlaz(r11));
  Registar32bit registar32bit_12 (.Ulaz(WriteData), .CLK(demultiplexer_1_out12), .RST(RST), .Izlaz(r12));
  Registar32bit registar32bit_13 (.Ulaz(WriteData), .CLK(demultiplexer_1_out13), .RST(RST), .Izlaz(r13));
  Registar32bit registar32bit_14 (.Ulaz(WriteData), .CLK(demultiplexer_1_out14), .RST(RST), .Izlaz(r14));
  Registar32bit registar32bit_15 (.Ulaz(WriteData), .CLK(demultiplexer_1_out15), .RST(RST), .Izlaz(r15));
  Registar32bit registar32bit_16 (.Ulaz(WriteData), .CLK(demultiplexer_1_out16), .RST(RST), .Izlaz(r16));
  Registar32bit registar32bit_17 (.Ulaz(WriteData), .CLK(demultiplexer_1_out17), .RST(RST), .Izlaz(r17));
  Registar32bit registar32bit_18 (.Ulaz(WriteData), .CLK(demultiplexer_1_out18), .RST(RST), .Izlaz(r18));
  Registar32bit registar32bit_19 (.Ulaz(WriteData), .CLK(demultiplexer_1_out19), .RST(RST), .Izlaz(r19));
  Registar32bit registar32bit_20 (.Ulaz(WriteData), .CLK(demultiplexer_1_out20), .RST(RST), .Izlaz(r20));
  Registar32bit registar32bit_21 (.Ulaz(WriteData), .CLK(demultiplexer_1_out21), .RST(RST), .Izlaz(r21));
  Registar32bit registar32bit_22 (.Ulaz(WriteData), .CLK(demultiplexer_1_out22), .RST(RST), .Izlaz(r22));
  Registar32bit registar32bit_23 (.Ulaz(WriteData), .CLK(demultiplexer_1_out23), .RST(RST), .Izlaz(r23));
  Registar32bit registar32bit_24 (.Ulaz(WriteData), .CLK(demultiplexer_1_out24), .RST(RST), .Izlaz(r24));
  Registar32bit registar32bit_25 (.Ulaz(WriteData), .CLK(demultiplexer_1_out25), .RST(RST), .Izlaz(r25));
  Registar32bit registar32bit_26 (.Ulaz(WriteData), .CLK(demultiplexer_1_out26), .RST(RST), .Izlaz(r26));
  Registar32bit registar32bit_27 (.Ulaz(WriteData), .CLK(demultiplexer_1_out27), .RST(RST), .Izlaz(r27));
  Registar32bit registar32bit_28 (.Ulaz(WriteData), .CLK(demultiplexer_1_out28), .RST(RST), .Izlaz(r28));
  Registar32bit registar32bit_29 (.Ulaz(WriteData), .CLK(demultiplexer_1_out29), .RST(RST), .Izlaz(r29));
  Registar32bit registar32bit_30 (.Ulaz(WriteData), .CLK(demultiplexer_1_out30), .RST(RST), .Izlaz(r30));
  Registar32bit registar32bit_31 (.Ulaz(WriteData), .CLK(demultiplexer_1_out31), .RST(RST), .Izlaz(r31));
  Multiplexer #(.select(5), .width(32)) multiplexer_1 (
    .in0({32{1'b0}}), .in1(r1), .in2(r2), .in3(r3), .in4(r4), .in5(r5), .in6(r6), .in7(r7), .in8(R8),
    .in9(r9), .in10(r10), .in11(r11), .in12(r12), .in13(r13), .in14(r14), .in15(r15), .in16(r16), .in17(r17),
    .in18(r18), .in19(r19), .in20(r20), .in21(r21), .in22(r22), .in23(r23), .in24(r24), .in25(r25),
    .in26(r26), .in27(r27), .in28(r28), .in29(r29), .in30(r30), .in31(r31), .out(ReadData1), .sel(ReadReg1));
  Multiplexer #(.select(5), .width(32)) multiplexer_2 (
    .in0({32{1'b0}}), .in1(r1), .in2(r2), .in3(r3), .in4(r4), .in5(r5), .in6(r6), .in7(r7), .in8(R8),
    .in9(r9), .in10(r10), .in11(r11), .in12(r12), .in13(r13), .in14(r14), .in15(r15), .in16(r16), .in17(r17),
    .in18(r18), .in19(r19), .in20(r20), .in21(r21), .in22(r22), .in23(r23), .in24(r24), .in25(r25),
    .in26(r26), .in27(r27), .in28(r28), .in29(r29), .in30(r30), .in31(r31), .out(ReadData2), .sel(ReadReg2));
endmodule

module Registar32bit (
  input  [31:0] Ulaz,
  input  CLK,
  input  RST,
  output [31:0] Izlaz
);

  Registar8bit registar8bit_1 (.Ulaz(Ulaz[7:0]), .RegWrite(CLK), .RST(RST), .out_4(Izlaz[7:0]));
  Registar8bit registar8bit_2 (.Ulaz(Ulaz[15:8]), .RegWrite(CLK), .RST(RST), .out_4(Izlaz[15:8]));
  Registar8bit registar8bit_3 (.Ulaz(Ulaz[23:16]), .RegWrite(CLK), .RST(RST), .out_4(Izlaz[23:16]));
  Registar8bit registar8bit_4 (.Ulaz(Ulaz[31:24]), .RegWrite(CLK), .RST(RST), .out_4(Izlaz[31:24]));
endmodule

module Registar8bit (
  input  [7:0] Ulaz,
  input  RegWrite,
  input  RST,
  output [7:0] out_4
);

  D_Flip_Flop d_ff_1 (.D(Ulaz[7]), .clk(RegWrite), .Q(out_4[7]), .reset(RST));  // open: Qn, preset
  D_Flip_Flop d_ff_2 (.D(Ulaz[6]), .clk(RegWrite), .Q(out_4[6]), .reset(RST));  // open: Qn, preset
  D_Flip_Flop d_ff_3 (.D(Ulaz[5]), .clk(RegWrite), .Q(out_4[5]), .reset(RST));  // open: Qn, preset
  D_Flip_Flop d_ff_4 (.D(Ulaz[4]), .clk(RegWrite), .Q(out_4[4]), .reset(RST));  // open: Qn, preset
  D_Flip_Flop d_ff_5 (.D(Ulaz[3]), .clk(RegWrite), .Q(out_4[3]), .reset(RST));  // open: Qn, preset
  D_Flip_Flop d_ff_6 (.D(Ulaz[2]), .clk(RegWrite), .Q(out_4[2]), .reset(RST));  // open: Qn, preset
  D_Flip_Flop d_ff_7 (.D(Ulaz[1]), .clk(RegWrite), .Q(out_4[1]), .reset(RST));  // open: Qn, preset
  D_Flip_Flop d_ff_8 (.D(Ulaz[0]), .clk(RegWrite), .Q(out_4[0]), .reset(RST));  // open: Qn, preset

  // Other names for the same wires on the sheet: CLK = RegWrite
endmodule

module Registar6bit (
  input  [5:0] Ulaz,
  input  RegWrite,
  input  RST,
  output [5:0] out_4
);

  D_Flip_Flop d_ff_1 (.D(Ulaz[5]), .Q(out_4[5]), .reset(RST));  // open: clk, Qn, preset
  D_Flip_Flop d_ff_2 (.D(Ulaz[4]), .clk(RegWrite), .Q(out_4[4]), .reset(RST));  // open: Qn, preset
  D_Flip_Flop d_ff_3 (.D(Ulaz[3]), .clk(RegWrite), .Q(out_4[3]), .reset(RST));  // open: Qn, preset
  D_Flip_Flop d_ff_4 (.D(Ulaz[2]), .clk(RegWrite), .Q(out_4[2]), .reset(RST));  // open: Qn, preset
  D_Flip_Flop d_ff_5 (.D(Ulaz[1]), .clk(RegWrite), .Q(out_4[1]), .reset(RST));  // open: Qn, preset
  D_Flip_Flop d_ff_6 (.D(Ulaz[0]), .clk(RegWrite), .Q(out_4[0]), .reset(RST));  // open: Qn, preset

  // Other names for the same wires on the sheet: CLK = RegWrite
endmodule

module Registar5bit (
  input  [4:0] Ulaz,
  input  RegWrite,
  input  RST,
  output [4:0] out_4
);

  D_Flip_Flop d_ff_1 (.D(Ulaz[4]), .clk(RegWrite), .Q(out_4[4]), .reset(RST));  // open: Qn, preset
  D_Flip_Flop d_ff_2 (.D(Ulaz[3]), .clk(RegWrite), .Q(out_4[3]), .reset(RST));  // open: Qn, preset
  D_Flip_Flop d_ff_3 (.D(Ulaz[2]), .clk(RegWrite), .Q(out_4[2]), .reset(RST));  // open: Qn, preset
  D_Flip_Flop d_ff_4 (.D(Ulaz[1]), .clk(RegWrite), .Q(out_4[1]), .reset(RST));  // open: Qn, preset
  D_Flip_Flop d_ff_5 (.D(Ulaz[0]), .clk(RegWrite), .Q(out_4[0]), .reset(RST));  // open: Qn, preset

  // Other names for the same wires on the sheet: CLK = RegWrite
endmodule

module PC (
  input  [31:0] Ulaz,
  input  PCWrite,
  input  CLK,
  input  RST,
  output [31:0] Izlaz
);

  wire and_1_out;

  and and_1 (and_1_out, PCWrite, CLK);
  Registar32bit registar32bit_1 (.Ulaz(Ulaz), .CLK(and_1_out), .RST(RST), .Izlaz(Izlaz));
endmodule

module IFIDReg (
  input  [31:0] PCplus4IF,
  input  [31:0] InstrukcijaIF,
  input  Flush,
  input  IFIDWrite,
  input  CLK,
  input  RST,
  output [31:0] PCplus4ID,
  output [31:0] InstrukcijaID
);

  wire CLK_t;
  wire [31:0] multiplexer_1_out, multiplexer_2_out;

  and and_1 (CLK_t, CLK, IFIDWrite);
  Multiplexer #(.width(32)) multiplexer_1 (.in0(PCplus4IF), .in1({32{1'b0}}), .out(multiplexer_1_out), .sel(Flush));
  Multiplexer #(.width(32)) multiplexer_2 (.in0(InstrukcijaIF), .in1({32{1'b0}}), .out(multiplexer_2_out), .sel(Flush));
  Registar32bit registar32bit_1 (.Ulaz(multiplexer_1_out), .CLK(CLK_t), .RST(RST), .Izlaz(PCplus4ID));
  Registar32bit registar32bit_2 (.Ulaz(multiplexer_2_out), .CLK(CLK_t), .RST(RST), .Izlaz(InstrukcijaID));
endmodule

module IDEXReg (
  input  [31:0] PCplus4ID,
  input  [31:0] ReadData1ID,
  input  [31:0] ReadData2ID,
  input  [31:0] SignExtID,
  input  RegDstID,
  input  [1:0] AluOpID,
  input  AluSrcID,
  input  LinkID,
  input  MemWriteID,
  input  MemReadID,
  input  RegWriteID,
  input  MemToRegID,
  input  [4:0] ID25do21,
  input  [4:0] ID20do16,
  input  [4:0] ID15do11,
  input  [1:0] StoreOpID,
  input  [2:0] LoadOpID,
  input  [5:0] OpID,
  input  [4:0] SaID,
  input  LinkRegID,
  input  Flush,
  input  CLK,
  input  RST,
  output [31:0] PCplus4EX,
  output [31:0] ReadData1EX,
  output [31:0] ReadData2EX,
  output [31:0] SignExtEX,
  output RegDstEX,
  output [1:0] AluOpEX,
  output AluSrcEX,
  output LinkEX,
  output MemWriteEX,
  output MemReadEX,
  output RegWriteEX,
  output MemToRegEX,
  output [4:0] EX25do21,
  output [4:0] EX20do16,
  output [4:0] EX15do11,
  output [1:0] StoreOpEx,
  output [2:0] LoadOpEx,
  output [5:0] OpEX,
  output [4:0] SaEX,
  output LinkRegEX
);

  wire multiplexer_6_out, multiplexer_7_out, multiplexer_8_out, multiplexer_9_out, multiplexer_10_out,
       multiplexer_11_out, multiplexer_12_out, multiplexer_13_out;
  wire [1:0] multiplexer_1_out, multiplexer_2_out;
  wire [2:0] multiplexer_3_out;
  wire [4:0] multiplexer_5_out, multiplexer_14_out, multiplexer_15_out, multiplexer_16_out;
  wire [5:0] multiplexer_4_out;
  wire [31:0] multiplexer_17_out, multiplexer_18_out, multiplexer_19_out, multiplexer_20_out;

  Multiplexer #(.width(2)) multiplexer_1 (.in0(AluOpID), .in1(2'b00), .out(multiplexer_1_out), .sel(Flush));
  Multiplexer #(.width(2)) multiplexer_2 (.in0(StoreOpID), .in1(2'b00), .out(multiplexer_2_out), .sel(Flush));
  Multiplexer #(.width(3)) multiplexer_3 (.in0(LoadOpID), .in1(3'b000), .out(multiplexer_3_out), .sel(Flush));
  Multiplexer #(.width(6)) multiplexer_4 (.in0(OpID), .in1({6{1'b0}}), .out(multiplexer_4_out), .sel(Flush));
  Multiplexer #(.width(5)) multiplexer_5 (.in0(SaID), .in1({5{1'b0}}), .out(multiplexer_5_out), .sel(Flush));
  Multiplexer multiplexer_6 (.in0(LinkRegID), .in1(1'b0), .out(multiplexer_6_out), .sel(Flush));
  Multiplexer multiplexer_7 (.in0(RegDstID), .in1(1'b0), .out(multiplexer_7_out), .sel(Flush));
  Multiplexer multiplexer_8 (.in0(AluSrcID), .in1(1'b0), .out(multiplexer_8_out), .sel(Flush));
  Multiplexer multiplexer_9 (.in0(LinkID), .in1(1'b0), .out(multiplexer_9_out), .sel(Flush));
  Multiplexer multiplexer_10 (.in0(MemWriteID), .in1(1'b0), .out(multiplexer_10_out), .sel(Flush));
  Multiplexer multiplexer_11 (.in0(MemReadID), .in1(1'b0), .out(multiplexer_11_out), .sel(Flush));
  Multiplexer multiplexer_12 (.in0(RegWriteID), .in1(1'b0), .out(multiplexer_12_out), .sel(Flush));
  Multiplexer multiplexer_13 (.in0(MemToRegID), .in1(1'b0), .out(multiplexer_13_out), .sel(Flush));
  Multiplexer #(.width(5)) multiplexer_14 (.in0(ID25do21), .in1({5{1'b0}}), .out(multiplexer_14_out), .sel(Flush));
  Multiplexer #(.width(5)) multiplexer_15 (.in0(ID20do16), .in1({5{1'b0}}), .out(multiplexer_15_out), .sel(Flush));
  Multiplexer #(.width(5)) multiplexer_16 (.in0(ID15do11), .in1({5{1'b0}}), .out(multiplexer_16_out), .sel(Flush));
  D_Flip_Flop d_ff_1 (.D(multiplexer_2_out[1]), .clk(CLK), .Q(StoreOpEx[1]), .reset(RST));  // open: Qn, preset
  D_Flip_Flop d_ff_2 (.D(multiplexer_3_out[2]), .clk(CLK), .Q(LoadOpEx[2]), .reset(RST));  // open: Qn, preset
  D_Flip_Flop d_ff_3 (.D(multiplexer_7_out), .clk(CLK), .Q(RegDstEX), .reset(RST));  // open: Qn, preset
  D_Flip_Flop d_ff_4 (.D(multiplexer_1_out[1]), .clk(CLK), .Q(AluOpEX[1]), .reset(RST));  // open: Qn, preset
  D_Flip_Flop d_ff_5 (.D(multiplexer_8_out), .clk(CLK), .Q(AluSrcEX), .reset(RST));  // open: Qn, preset
  D_Flip_Flop d_ff_6 (.D(multiplexer_9_out), .clk(CLK), .Q(LinkEX), .reset(RST));  // open: Qn, preset
  D_Flip_Flop d_ff_7 (.D(multiplexer_10_out), .clk(CLK), .Q(MemWriteEX), .reset(RST));  // open: Qn, preset
  D_Flip_Flop d_ff_8 (.D(multiplexer_11_out), .clk(CLK), .Q(MemReadEX), .reset(RST));  // open: Qn, preset
  D_Flip_Flop d_ff_9 (.D(multiplexer_12_out), .clk(CLK), .Q(RegWriteEX), .reset(RST));  // open: Qn, preset
  D_Flip_Flop d_ff_10 (.D(multiplexer_13_out), .clk(CLK), .Q(MemToRegEX), .reset(RST));  // open: Qn, preset
  D_Flip_Flop d_ff_11 (.D(multiplexer_6_out), .clk(CLK), .Q(LinkRegEX), .reset(RST));  // open: Qn, preset
  Multiplexer #(.width(32)) multiplexer_17 (.in0(PCplus4ID), .in1({32{1'b0}}), .out(multiplexer_17_out), .sel(Flush));
  Multiplexer #(.width(32)) multiplexer_18 (.in0(ReadData1ID), .in1({32{1'b0}}), .out(multiplexer_18_out), .sel(Flush));
  Multiplexer #(.width(32)) multiplexer_19 (.in0(ReadData2ID), .in1({32{1'b0}}), .out(multiplexer_19_out), .sel(Flush));
  Multiplexer #(.width(32)) multiplexer_20 (.in0(SignExtID), .in1({32{1'b0}}), .out(multiplexer_20_out), .sel(Flush));
  D_Flip_Flop d_ff_12 (.D(multiplexer_1_out[0]), .clk(CLK), .Q(AluOpEX[0]), .reset(RST));  // open: Qn, preset
  D_Flip_Flop d_ff_13 (.D(multiplexer_2_out[0]), .clk(CLK), .Q(StoreOpEx[0]), .reset(RST));  // open: Qn, preset
  D_Flip_Flop d_ff_14 (.D(multiplexer_3_out[1]), .clk(CLK), .Q(LoadOpEx[1]), .reset(RST));  // open: Qn, preset
  Registar6bit registar6bit_1 (.Ulaz(multiplexer_4_out), .RegWrite(CLK), .RST(RST), .out_4(OpEX));
  Registar5bit registar5bit_1 (.Ulaz(multiplexer_14_out), .RegWrite(CLK), .RST(RST), .out_4(EX25do21));
  Registar5bit registar5bit_2 (.Ulaz(multiplexer_15_out), .RegWrite(CLK), .RST(RST), .out_4(EX20do16));
  Registar5bit registar5bit_3 (.Ulaz(multiplexer_16_out), .RegWrite(CLK), .RST(RST), .out_4(EX15do11));
  Registar5bit registar5bit_4 (.Ulaz(multiplexer_5_out), .RegWrite(CLK), .RST(RST), .out_4(SaEX));
  D_Flip_Flop d_ff_15 (.D(multiplexer_3_out[0]), .clk(CLK), .Q(LoadOpEx[0]), .reset(RST));  // open: Qn, preset
  Registar32bit registar32bit_1 (.Ulaz(multiplexer_17_out), .CLK(CLK), .RST(RST), .Izlaz(PCplus4EX));
  Registar32bit registar32bit_2 (.Ulaz(multiplexer_18_out), .CLK(CLK), .RST(RST), .Izlaz(ReadData1EX));
  Registar32bit registar32bit_3 (.Ulaz(multiplexer_19_out), .CLK(CLK), .RST(RST), .Izlaz(ReadData2EX));
  Registar32bit registar32bit_4 (.Ulaz(multiplexer_20_out), .CLK(CLK), .RST(RST), .Izlaz(SignExtEX));
endmodule

module EXMEMReg (
  input  [31:0] ALUrezEX,
  input  [31:0] ReadData2EX,
  input  [4:0] WriteRegisterEX,
  input  RegWriteEX,
  input  MemToRegEX,
  input  MemReadEX,
  input  MemWriteEX,
  input  [1:0] StoreOpEx,
  input  [2:0] LoadOpEx,
  input  Flush,
  input  CLK,
  input  RST,
  output [31:0] ALUrezMEM,
  output [31:0] ReadData2MEM,
  output [4:0] WriteRegisterMEM,
  output RegWriteMEM,
  output MemToRegMEM,
  output MemReadMEM,
  output MemWriteMEM,
  output [1:0] StoreOpMem,
  output [2:0] LoadOpMem
);

  wire [1:0] multiplexer_1_out;
  wire [2:0] multiplexer_2_out;
  wire [2:2] registar5bit_2_out_4;
  wire [4:0] multiplexer_5_out, multiplexer_6_out;
  wire [31:0] multiplexer_3_out, multiplexer_4_out;

  Multiplexer #(.width(2)) multiplexer_1 (.in0(StoreOpEx), .in1(2'b00), .out(multiplexer_1_out), .sel(Flush));
  Multiplexer #(.width(3)) multiplexer_2 (.in0(LoadOpEx), .in1(3'b000), .out(multiplexer_2_out), .sel(Flush));
  Multiplexer #(.width(32)) multiplexer_3 (.in0(ALUrezEX), .in1({32{1'b0}}), .out(multiplexer_3_out), .sel(Flush));
  Multiplexer #(.width(32)) multiplexer_4 (.in0(ReadData2EX), .in1({32{1'b0}}), .out(multiplexer_4_out), .sel(Flush));
  Multiplexer #(.width(5)) multiplexer_5 (.in0(WriteRegisterEX), .in1({5{1'b0}}), .out(multiplexer_5_out), .sel(Flush));
  Multiplexer #(.width(5)) multiplexer_6 (
    .in0({MemWriteEX, MemReadEX, 1'b1, MemToRegEX, RegWriteEX}), .in1({5{1'b0}}), .out(multiplexer_6_out),
    .sel(Flush));
  D_Flip_Flop d_ff_1 (.D(multiplexer_1_out[1]), .clk(CLK), .Q(StoreOpMem[1]), .reset(RST));  // open: Qn, preset
  D_Flip_Flop d_ff_2 (.D(multiplexer_2_out[2]), .clk(CLK), .Q(LoadOpMem[2]), .reset(RST));  // open: Qn, preset
  D_Flip_Flop d_ff_3 (.D(multiplexer_1_out[0]), .clk(CLK), .Q(StoreOpMem[0]), .reset(RST));  // open: Qn, preset
  Registar32bit registar32bit_1 (.Ulaz(multiplexer_3_out), .CLK(CLK), .RST(RST), .Izlaz(ALUrezMEM));
  Registar32bit registar32bit_2 (.Ulaz(multiplexer_4_out), .CLK(CLK), .RST(RST), .Izlaz(ReadData2MEM));
  Registar5bit registar5bit_1 (.Ulaz(multiplexer_5_out), .RegWrite(CLK), .RST(RST), .out_4(WriteRegisterMEM));
  Registar5bit registar5bit_2 (
    .Ulaz(multiplexer_6_out), .RegWrite(CLK), .RST(RST),
    .out_4({MemWriteMEM, MemReadMEM, registar5bit_2_out_4[2], MemToRegMEM, RegWriteMEM}));
  D_Flip_Flop d_ff_4 (.D(multiplexer_2_out[1]), .clk(CLK), .Q(LoadOpMem[1]), .reset(RST));  // open: Qn, preset
  D_Flip_Flop d_ff_5 (.D(multiplexer_2_out[0]), .clk(CLK), .Q(LoadOpMem[0]), .reset(RST));  // open: Qn, preset
endmodule

module MEMWBReg (
  input  [31:0] ALUrezMEM,
  input  [31:0] ReadDataMEM,
  input  RegWriteMEM,
  input  MemToRegMEM,
  input  [4:0] OdredisnaAdresaMEM,
  input  CLK,
  input  RST,
  output [31:0] ALUrezWB,
  output [31:0] ReadDataWB,
  output RegWriteWB,
  output MemToRegWB,
  output [4:0] OdredisnaAdresaWB
);

  D_Flip_Flop d_ff_1 (.D(RegWriteMEM), .clk(CLK), .Q(RegWriteWB), .reset(RST));  // open: Qn, preset
  D_Flip_Flop d_ff_2 (.D(MemToRegMEM), .clk(CLK), .Q(MemToRegWB), .reset(RST));  // open: Qn, preset
  Registar32bit registar32bit_1 (.Ulaz(ALUrezMEM), .CLK(CLK), .RST(RST), .Izlaz(ALUrezWB));
  Registar32bit registar32bit_2 (.Ulaz(ReadDataMEM), .CLK(CLK), .RST(RST), .Izlaz(ReadDataWB));
  Registar5bit registar5bit_1 (.Ulaz(OdredisnaAdresaMEM), .RegWrite(CLK), .RST(RST), .out_4(OdredisnaAdresaWB));
endmodule

module ADD1b (
  input  A,
  input  B,
  input  Prijenos,
  output R,
  output PrijenosO
);

  wire and_1_out, and_2_out, and_3_out, and_4_out, and_5_out, and_6_out, and_7_out, not_1_out, not_2_out,
       not_3_out;

  not not_1 (not_1_out, A);
  not not_2 (not_2_out, B);
  not not_3 (not_3_out, Prijenos);
  and and_1 (and_1_out, not_1_out, not_2_out, Prijenos);
  and and_2 (and_2_out, not_1_out, B, not_3_out);
  and and_3 (and_3_out, A, not_2_out, not_3_out);
  and and_4 (and_4_out, A, B, Prijenos);
  and and_5 (and_5_out, B, Prijenos);
  and and_6 (and_6_out, A, Prijenos);
  and and_7 (and_7_out, A, B);
  or or_1 (R, and_1_out, and_2_out, and_3_out, and_4_out);
  or or_2 (PrijenosO, and_5_out, and_6_out, and_7_out);
endmodule

module ADD8bit (
  input  [7:0] A,
  input  [7:0] B,
  input  PrijenosIN,
  output [7:0] R,
  output PrijenosOUT
);

  wire add1b_2_prijenoso, add1b_3_prijenoso, add1b_4_prijenoso, add1b_5_prijenoso, add1b_6_prijenoso,
       add1b_7_prijenoso, add1b_8_prijenoso;

  ADD1b add1b_1 (.A(A[7]), .B(B[7]), .Prijenos(add1b_2_prijenoso), .R(R[7]), .PrijenosO(PrijenosOUT));
  ADD1b add1b_2 (.A(A[6]), .B(B[6]), .Prijenos(add1b_3_prijenoso), .R(R[6]), .PrijenosO(add1b_2_prijenoso));
  ADD1b add1b_3 (.A(A[5]), .B(B[5]), .Prijenos(add1b_4_prijenoso), .R(R[5]), .PrijenosO(add1b_3_prijenoso));
  ADD1b add1b_4 (.A(A[4]), .B(B[4]), .Prijenos(add1b_5_prijenoso), .R(R[4]), .PrijenosO(add1b_4_prijenoso));
  ADD1b add1b_5 (.A(A[3]), .B(B[3]), .Prijenos(add1b_6_prijenoso), .R(R[3]), .PrijenosO(add1b_5_prijenoso));
  ADD1b add1b_6 (.A(A[2]), .B(B[2]), .Prijenos(add1b_7_prijenoso), .R(R[2]), .PrijenosO(add1b_6_prijenoso));
  ADD1b add1b_7 (.A(A[1]), .B(B[1]), .Prijenos(add1b_8_prijenoso), .R(R[1]), .PrijenosO(add1b_7_prijenoso));
  ADD1b add1b_8 (.A(A[0]), .B(B[0]), .Prijenos(PrijenosIN), .R(R[0]), .PrijenosO(add1b_8_prijenoso));

  // Other names for the same wires on the sheet: p = PrijenosIN
endmodule

module ADD32bit (
  input  [31:0] in_1,
  input  [31:0] in_2,
  output [31:0] out_3,
  output out_4
);

  wire add8bit_2_prijenosout, add8bit_3_prijenosout, add8bit_4_prijenosout;

  ADD8bit add8bit_1 (
    .A(in_1[31:24]), .B(in_2[31:24]), .PrijenosIN(add8bit_2_prijenosout), .R(out_3[31:24]),
    .PrijenosOUT(out_4));
  ADD8bit add8bit_2 (
    .A(in_1[23:16]), .B(in_2[23:16]), .PrijenosIN(add8bit_3_prijenosout), .R(out_3[23:16]),
    .PrijenosOUT(add8bit_2_prijenosout));
  ADD8bit add8bit_3 (
    .A(in_1[15:8]), .B(in_2[15:8]), .PrijenosIN(add8bit_4_prijenosout), .R(out_3[15:8]),
    .PrijenosOUT(add8bit_3_prijenosout));
  ADD8bit add8bit_4 (
    .A(in_1[7:0]), .B(in_2[7:0]), .PrijenosIN(1'b0), .R(out_3[7:0]), .PrijenosOUT(add8bit_4_prijenosout));

  // Other names for the same wires on the sheet: Izuzetak = out_4
endmodule

module SUB1b (
  input  A,
  input  B,
  input  Posudba,
  output R,
  output PosudbaO
);

  wire and_1_out, and_2_out, and_3_out, and_4_out, and_5_out, and_6_out, and_7_out, not_1_out, not_2_out,
       not_3_out;

  not not_1 (not_1_out, A);
  not not_2 (not_2_out, B);
  not not_3 (not_3_out, Posudba);
  and and_1 (and_1_out, not_1_out, not_2_out, Posudba);
  and and_2 (and_2_out, not_1_out, B, not_3_out);
  and and_3 (and_3_out, A, not_2_out, not_3_out);
  and and_4 (and_4_out, A, B, Posudba);
  and and_5 (and_5_out, not_1_out, Posudba);
  and and_6 (and_6_out, not_1_out, B);
  and and_7 (and_7_out, B, Posudba);
  or or_1 (R, and_1_out, and_2_out, and_3_out, and_4_out);
  or or_2 (PosudbaO, and_5_out, and_6_out, and_7_out);
endmodule

module SUB8bit (
  input  [7:0] A,
  input  [7:0] B,
  input  PosudbaIN,
  output [7:0] R,
  output PosudbaOUT
);

  wire sub1b_2_posudbao, sub1b_3_posudbao, sub1b_4_posudbao, sub1b_5_posudbao, sub1b_6_posudbao,
       sub1b_7_posudbao, sub1b_8_posudbao;

  SUB1b sub1b_1 (.A(A[7]), .B(B[7]), .Posudba(sub1b_2_posudbao), .R(R[7]), .PosudbaO(PosudbaOUT));
  SUB1b sub1b_2 (.A(A[6]), .B(B[6]), .Posudba(sub1b_3_posudbao), .R(R[6]), .PosudbaO(sub1b_2_posudbao));
  SUB1b sub1b_3 (.A(A[5]), .B(B[5]), .Posudba(sub1b_4_posudbao), .R(R[5]), .PosudbaO(sub1b_3_posudbao));
  SUB1b sub1b_4 (.A(A[4]), .B(B[4]), .Posudba(sub1b_5_posudbao), .R(R[4]), .PosudbaO(sub1b_4_posudbao));
  SUB1b sub1b_5 (.A(A[3]), .B(B[3]), .Posudba(sub1b_6_posudbao), .R(R[3]), .PosudbaO(sub1b_5_posudbao));
  SUB1b sub1b_6 (.A(A[2]), .B(B[2]), .Posudba(sub1b_7_posudbao), .R(R[2]), .PosudbaO(sub1b_6_posudbao));
  SUB1b sub1b_7 (.A(A[1]), .B(B[1]), .Posudba(sub1b_8_posudbao), .R(R[1]), .PosudbaO(sub1b_7_posudbao));
  SUB1b sub1b_8 (.A(A[0]), .B(B[0]), .Posudba(PosudbaIN), .R(R[0]), .PosudbaO(sub1b_8_posudbao));

  // Other names for the same wires on the sheet: p = PosudbaIN
endmodule

module SUB32bit (
  input  [31:0] A,
  input  [31:0] B,
  output [31:0] R,
  output out_4
);

  wire sub8bit_2_posudbaout, sub8bit_3_posudbaout, sub8bit_4_posudbaout;

  SUB8bit sub8bit_1 (.A(A[31:24]), .B(B[31:24]), .PosudbaIN(sub8bit_2_posudbaout), .R(R[31:24]), .PosudbaOUT(out_4));
  SUB8bit sub8bit_2 (
    .A(A[23:16]), .B(B[23:16]), .PosudbaIN(sub8bit_3_posudbaout), .R(R[23:16]),
    .PosudbaOUT(sub8bit_2_posudbaout));
  SUB8bit sub8bit_3 (
    .A(A[15:8]), .B(B[15:8]), .PosudbaIN(sub8bit_4_posudbaout), .R(R[15:8]), .PosudbaOUT(sub8bit_3_posudbaout));
  SUB8bit sub8bit_4 (.A(A[7:0]), .B(B[7:0]), .PosudbaIN(1'b0), .R(R[7:0]), .PosudbaOUT(sub8bit_4_posudbaout));

  // Other names for the same wires on the sheet: Izuzetak = out_4
endmodule

module SLTU1b (
  input  A,
  input  B,
  input  C,
  output P
);

  wire and_1_out, and_2_out, and_3_out, not_1_out;

  not not_1 (not_1_out, A);
  and and_1 (and_1_out, not_1_out, C);
  and and_2 (and_2_out, not_1_out, B);
  or or_1 (P, and_1_out, and_2_out, and_3_out);
  and and_3 (and_3_out, B, C);
endmodule

module SLTU8bit (
  input  [7:0] A,
  input  [7:0] B,
  input  C,
  output P
);

  wire sltu1b_2_p, sltu1b_3_p, sltu1b_4_p, sltu1b_5_p, sltu1b_6_p, sltu1b_7_p, sltu1b_8_p;

  SLTU1b sltu1b_1 (.A(A[7]), .B(B[7]), .C(sltu1b_2_p), .P(P));
  SLTU1b sltu1b_2 (.A(A[6]), .B(B[6]), .C(sltu1b_3_p), .P(sltu1b_2_p));
  SLTU1b sltu1b_3 (.A(A[5]), .B(B[5]), .C(sltu1b_4_p), .P(sltu1b_3_p));
  SLTU1b sltu1b_4 (.A(A[4]), .B(B[4]), .C(sltu1b_5_p), .P(sltu1b_4_p));
  SLTU1b sltu1b_5 (.A(A[3]), .B(B[3]), .C(sltu1b_6_p), .P(sltu1b_5_p));
  SLTU1b sltu1b_6 (.A(A[2]), .B(B[2]), .C(sltu1b_7_p), .P(sltu1b_6_p));
  SLTU1b sltu1b_7 (.A(A[1]), .B(B[1]), .C(sltu1b_8_p), .P(sltu1b_7_p));
  SLTU1b sltu1b_8 (.A(A[0]), .B(B[0]), .C(C), .P(sltu1b_8_p));
endmodule

module SLTU32bit (
  input  [31:0] A,
  input  [31:0] B,
  output SLTU
);

  wire sltu8bit_2_p, sltu8bit_3_p, sltu8bit_4_p;

  SLTU8bit sltu8bit_1 (.A(A[31:24]), .B(B[31:24]), .C(sltu8bit_2_p), .P(SLTU));
  SLTU8bit sltu8bit_2 (.A(A[23:16]), .B(B[23:16]), .C(sltu8bit_3_p), .P(sltu8bit_2_p));
  SLTU8bit sltu8bit_3 (.A(A[15:8]), .B(B[15:8]), .C(sltu8bit_4_p), .P(sltu8bit_3_p));
  SLTU8bit sltu8bit_4 (.A(A[7:0]), .B(B[7:0]), .C(1'b0), .P(sltu8bit_4_p));
endmodule

module SLT32b (
  input  [31:0] A,
  input  [31:0] B,
  output SLT
);

  wire sltu32bit_1_sltu;

  SLTU32bit sltu32bit_1 (.A(A), .B(B), .SLTU(sltu32bit_1_sltu));
  Multiplexer #(.select(2)) multiplexer_1 (
    .in0(sltu32bit_1_sltu), .in1(1'b1), .in2(1'b0), .in3(sltu32bit_1_sltu), .out(SLT), .sel({B[31], A[31]}));
endmodule

module noviALU32bit (
  input  [31:0] A,
  input  [31:0] B,
  input  [3:0] ALUControl,
  input  [4:0] Sa,
  input  SV,
  output [31:0] ALUresult,
  output ZeroFlag,
  output Overflow
);

  wire AddOverflow, and_1_out, and_2_out, and_4_out, and_5_out, not_1_out, not_2_out, not_3_out, not_4_out,
       not_5_out, not_6_out, SubOverflow;
  wire [0:0] SLT1, SLTU1;
  wire [4:0] multiplexer_2_out;
  wire [31:0] ADD1, AND1, NOR1, OR1, SLL1, SRA1, SRL1, SUB1, XOR1;

  not not_1 (not_1_out, A[31]);
  not not_2 (not_2_out, B[31]);
  not not_3 (not_3_out, ALUresult[31]);
  and and_1 (and_1_out, not_1_out, not_2_out, ALUresult[31]);
  and and_2 (and_2_out, A[31], B[31], not_3_out);
  Multiplexer #(.select(4), .width(32)) multiplexer_1 (
    .in0(AND1), .in1(OR1), .in2(ADD1), .in3(SLL1), .in4(SRL1), .in5(SRA1), .in6(SUB1),
    .in7({{31{1'b0}}, SLT1[0]}), .in8({{31{1'b0}}, SLTU1[0]}), .in9({B[15:0], {16{1'b0}}}), .in12(NOR1),
    .in13(XOR1), .out(ALUresult), .sel(ALUControl));  // open: in10, in11, in14, in15
  EQ32bit eq32bit_1 (.A(ALUresult), .B({32{1'b0}}), .EQ(ZeroFlag));
  Multiplexer #(.width(5)) multiplexer_2 (.in0(Sa), .in1(A[4:0]), .out(multiplexer_2_out), .sel(SV));
  Multiplexer #(.select(4)) multiplexer_3 (
    .in0(1'b0), .in1(1'b0), .in2(AddOverflow), .in3(1'b0), .in4(1'b0), .in5(1'b0), .in6(SubOverflow),
    .in7(1'b0), .in8(1'b0), .in9(1'b0), .in10(1'b0), .in11(1'b0), .in12(1'b0), .in13(1'b0), .in14(1'b0),
    .in15(1'b0), .out(Overflow), .sel(ALUControl));
  or or_1 (AddOverflow, and_1_out, and_2_out);
  assign AND1 = A & B;  // AND_Gate and_3, 32 bits wide
  assign OR1 = A | B;  // OR_Gate or_2, 32 bits wide
  not not_4 (not_4_out, A[31]);
  assign NOR1 = ~(A | B);  // NOR_Gate nor_1, 32 bits wide
  assign XOR1 = A ^ B;  // XOR_Gate xor_1, 32 bits wide
  not not_5 (not_5_out, B[31]);
  not not_6 (not_6_out, ALUresult[31]);
  ADD32bit add32bit_1 (.in_1(A), .in_2(B), .out_3(ADD1));  // open: out_4
  SUB32bit sub32bit_1 (.A(A), .B(B), .R(SUB1));  // open: out_4
  SLT32b slt32b_1 (.A(A), .B(B), .SLT(SLT1[0]));
  SLTU32bit sltu32bit_1 (.A(A), .B(B), .SLTU(SLTU1[0]));
  SLL32bit sll32bit_1 (.Ulaz(B), .Ctrl(multiplexer_2_out), .Izlaz(SLL1));
  SRL32bit srl32bit_1 (.Ulaz(B), .Ctrl(multiplexer_2_out), .Izlaz(SRL1));
  SRA32 sra32_1 (.Ulaz(B), .Ctrl(multiplexer_2_out), .Izlaz(SRA1));
  and and_4 (and_4_out, not_4_out, B[31], ALUresult[31]);
  and and_5 (and_5_out, A[31], not_5_out, not_6_out);
  or or_3 (SubOverflow, and_4_out, and_5_out);

  // Other names for the same wires on the sheet: ALURez[31:0] = ALUresult; LUI1[31:16] = B[15:0]
endmodule

module ALU1bit (
  input  A,
  input  B,
  input  C,
  input  [3:0] ALUControl,
  input  ZIn,
  output Izlaz,
  output ZOut,
  output P
);

  wire ADDP, ADDR, AND1, NOR1, not_1_out, OR1, SLTP, SUBP, SUBR, XOR1;

  nor nor_1 (NOR1, A, B);
  xor xor_1 (XOR1, A, B);
  and and_1 (AND1, A, B);
  or or_1 (OR1, A, B);
  ADD1b add1b_1 (.A(A), .B(B), .Prijenos(C), .R(ADDR), .PrijenosO(ADDP));
  SUB1b sub1b_1 (.A(A), .B(B), .Posudba(C), .R(SUBR), .PosudbaO(SUBP));
  SLTU1b sltu1b_1 (.A(A), .B(B), .C(C), .P(SLTP));
  Multiplexer #(.select(4)) multiplexer_1 (
    .in0(AND1), .in1(OR1), .in2(ADDR), .in3(1'b0), .in4(1'b0), .in5(1'b0), .in6(SUBR), .in7(1'b0),
    .in8(1'b0), .in9(1'b0), .in10(1'b0), .in11(1'b0), .in12(NOR1), .in13(1'b0), .in14(1'b0), .in15(1'b0),
    .out(Izlaz), .sel(ALUControl));
  not not_1 (not_1_out, Izlaz);
  and and_2 (ZOut, not_1_out, ZIn);
  Multiplexer #(.select(4)) multiplexer_2 (
    .in0(1'b0), .in1(1'b0), .in2(ADDP), .in3(1'b0), .in4(1'b0), .in5(1'b0), .in6(SUBP), .in7(SLTP),
    .in8(1'b0), .in9(1'b0), .in10(1'b0), .in11(1'b0), .in12(1'b0), .in13(1'b0), .in14(1'b0), .in15(1'b0),
    .out(P), .sel(ALUControl));
endmodule

module ALU8bit (
  input  [7:0] A,
  input  [7:0] B,
  input  C,
  input  ZIn,
  input  [3:0] ALUControl,
  output ZOut,
  output P,
  output [7:0] R
);

  wire alu1bit_2_p, alu1bit_2_zout, alu1bit_3_p, alu1bit_3_zout, alu1bit_4_p, alu1bit_4_zout, alu1bit_5_p,
       alu1bit_5_zout, alu1bit_6_p, alu1bit_6_zout, alu1bit_7_p, alu1bit_7_zout, alu1bit_8_p, alu1bit_8_zout;

  ALU1bit alu1bit_1 (
    .A(A[7]), .B(B[7]), .C(alu1bit_2_p), .ALUControl(ALUControl), .ZIn(alu1bit_2_zout), .Izlaz(R[7]),
    .ZOut(ZOut), .P(P));
  ALU1bit alu1bit_2 (
    .A(A[6]), .B(B[6]), .C(alu1bit_3_p), .ALUControl(ALUControl), .ZIn(alu1bit_3_zout), .Izlaz(R[6]),
    .ZOut(alu1bit_2_zout), .P(alu1bit_2_p));
  ALU1bit alu1bit_3 (
    .A(A[5]), .B(B[5]), .C(alu1bit_4_p), .ALUControl(ALUControl), .ZIn(alu1bit_4_zout), .Izlaz(R[5]),
    .ZOut(alu1bit_3_zout), .P(alu1bit_3_p));
  ALU1bit alu1bit_4 (
    .A(A[4]), .B(B[4]), .C(alu1bit_5_p), .ALUControl(ALUControl), .ZIn(alu1bit_5_zout), .Izlaz(R[4]),
    .ZOut(alu1bit_4_zout), .P(alu1bit_4_p));
  ALU1bit alu1bit_5 (
    .A(A[3]), .B(B[3]), .C(alu1bit_6_p), .ALUControl(ALUControl), .ZIn(alu1bit_6_zout), .Izlaz(R[3]),
    .ZOut(alu1bit_5_zout), .P(alu1bit_5_p));
  ALU1bit alu1bit_6 (
    .A(A[2]), .B(B[2]), .C(alu1bit_7_p), .ALUControl(ALUControl), .ZIn(alu1bit_7_zout), .Izlaz(R[2]),
    .ZOut(alu1bit_6_zout), .P(alu1bit_6_p));
  ALU1bit alu1bit_7 (
    .A(A[1]), .B(B[1]), .C(alu1bit_8_p), .ALUControl(ALUControl), .ZIn(alu1bit_8_zout), .Izlaz(R[1]),
    .ZOut(alu1bit_7_zout), .P(alu1bit_7_p));
  ALU1bit alu1bit_8 (
    .A(A[0]), .B(B[0]), .C(C), .ALUControl(ALUControl), .ZIn(ZIn), .Izlaz(R[0]), .ZOut(alu1bit_8_zout),
    .P(alu1bit_8_p));
endmodule

module ALU32bit (
  input  [31:0] A,
  input  [31:0] B,
  input  [3:0] ALUControl,
  output [31:0] ALUResult,
  output ZeroFlag
);

  wire alu8bit_2_p, alu8bit_2_zout, alu8bit_3_p, alu8bit_3_zout, alu8bit_4_p, alu8bit_4_zout, and_1_out,
       not_1_out, not_2_out, ZF;
  wire [0:0] alu8bit_1_p;
  wire [31:0] alu8bit_4_r;

  Multiplexer #(.width(32)) multiplexer_1 (
    .in0(alu8bit_4_r), .in1({{31{1'b0}}, alu8bit_1_p[0]}), .out(ALUResult), .sel(and_1_out));
  Multiplexer multiplexer_2 (.in0(ZF), .in1(not_1_out), .out(ZeroFlag), .sel(and_1_out));
  not not_1 (not_1_out, alu8bit_1_p[0]);
  ALU8bit alu8bit_1 (
    .A(A[31:24]), .B(B[31:24]), .C(alu8bit_2_p), .ZIn(alu8bit_2_zout), .ALUControl(ALUControl), .ZOut(ZF),
    .P(alu8bit_1_p[0]), .R(alu8bit_4_r[31:24]));
  and and_1 (and_1_out, not_2_out, ALUControl[2], ALUControl[1], ALUControl[0]);
  not not_2 (not_2_out, ALUControl[3]);
  ALU8bit alu8bit_2 (
    .A(A[23:16]), .B(B[23:16]), .C(alu8bit_3_p), .ZIn(alu8bit_3_zout), .ALUControl(ALUControl),
    .ZOut(alu8bit_2_zout), .P(alu8bit_2_p), .R(alu8bit_4_r[23:16]));
  ALU8bit alu8bit_3 (
    .A(A[15:8]), .B(B[15:8]), .C(alu8bit_4_p), .ZIn(alu8bit_4_zout), .ALUControl(ALUControl),
    .ZOut(alu8bit_3_zout), .P(alu8bit_3_p), .R(alu8bit_4_r[15:8]));
  ALU8bit alu8bit_4 (
    .A(A[7:0]), .B(B[7:0]), .ZIn(1'b1), .ALUControl(ALUControl), .ZOut(alu8bit_4_zout), .P(alu8bit_4_p),
    .R(alu8bit_4_r[7:0]));  // open: C
endmodule

module pom (
  input  i1,
  input  i2,
  input  i3,
  input  i4,
  input  i5,
  input  i6,
  output o1
);

  wire and_1_out, and_2_out, not_1_out, not_2_out, not_3_out, not_4_out;

  not not_1 (not_1_out, i1);
  not not_2 (not_2_out, i2);
  not not_3 (not_3_out, i3);
  not not_4 (not_4_out, i6);
  and and_1 (and_1_out, not_1_out, not_2_out, not_3_out, i4, not_4_out);
  and and_2 (and_2_out, not_1_out, not_2_out, not_3_out, i4, i5);
  or or_1 (o1, and_1_out, and_2_out);
endmodule

module ALUControl (
  input  [1:0] ALUOp,
  input  [5:0] Instr,
  input  [5:0] Op,
  output [3:0] ALUControl,
  output SV,
  output Invalid
);

  wire and_1_out, and_2_out, and_3_out, and_4_out, and_5_out, not_1_out, not_2_out, not_3_out, not_4_out,
       not_5_out, not_6_out, or_1_out;
  wire [3:0] ICtrl, RCtrl;

  not not_1 (not_1_out, Instr[5]);
  not not_2 (not_2_out, Instr[4]);
  not not_3 (not_3_out, Instr[3]);
  not not_4 (not_4_out, Instr[0]);
  ROM #(.addrWidth(6), .dataWidth(4)) rom_1 (.addr(Instr), .data(RCtrl));
  ROM #(.addrWidth(6), .dataWidth(4)) rom_2 (.addr(Op), .data(ICtrl));
  and and_1 (and_1_out, RCtrl[0], RCtrl[1], RCtrl[2], RCtrl[3]);
  and and_2 (and_2_out, ICtrl[0], ICtrl[1], ICtrl[2], ICtrl[3]);
  and and_3 (and_3_out, not_1_out, not_2_out, not_3_out, Instr[2], not_4_out);
  and and_4 (and_4_out, not_1_out, not_2_out, not_3_out, Instr[2], Instr[1]);
  not not_5 (not_5_out, ALUOp[0]);
  or or_1 (or_1_out, and_3_out, and_4_out);
  and and_5 (and_5_out, and_1_out, ALUOp[1], not_5_out);
  not not_6 (not_6_out, ALUOp[0]);
  or or_2 (Invalid, and_5_out, and_2_out);
  and and_6 (SV, not_6_out, ALUOp[1], or_1_out);
  Multiplexer #(.select(2), .width(4)) multiplexer_1 (
    .in0(4'b0010), .in1(4'b0110), .in2(RCtrl), .in3(ICtrl), .out(ALUControl), .sel(ALUOp));

  // Notes on the sheet:
  //   contents of rom_1 (hex, n*v repeats v):
  //   3 f 4 5 3 f 4 5 0 0 f f 0 0 f f 4*0 4*f 4*0 4*f 2 2 6 6 0 1 d c f f 7 8 20*f
  //   contents of rom_2 (hex, n*v repeats v):
  //   8*0 2 2 7 8 0 1 d 9 0 15*f 0 0 f 0 0 0 f f 0 0 f 0 20*f
endmodule

module Control (
  input  [5:0] Ulaz,
  output RegDst,
  output Jump,
  output Branch,
  output MemRead,
  output MemToReg,
  output [1:0] ALUOp,
  output MemWrite,
  output ALUSrc,
  output RegWrite
);

  wire and_7_out, and_8_out, not_1_out, not_2_out, not_3_out, not_4_out;

  not not_1 (not_1_out, Ulaz[3]);
  not not_2 (not_2_out, Ulaz[2]);
  not not_3 (not_3_out, Ulaz[1]);
  not not_4 (not_4_out, Ulaz[0]);
  and and_1 (RegDst, not_1_out, not_3_out);
  and and_2 (Jump, Ulaz[1], not_4_out);
  and and_3 (MemRead, not_1_out, Ulaz[0]);
  and and_4 (MemToReg, not_1_out, Ulaz[0]);
  and and_5 (ALUOp[1], not_1_out, not_2_out, not_3_out);
  and and_6 (MemWrite, Ulaz[3], Ulaz[1]);
  or or_1 (ALUSrc, Ulaz[3], Ulaz[0]);
  and and_7 (and_7_out, not_2_out, not_3_out);
  and and_8 (and_8_out, not_1_out, Ulaz[0]);
  or or_2 (RegWrite, and_7_out, and_8_out);

  assign ALUOp[0] = Ulaz[2];
  assign Branch = Ulaz[2];
endmodule

module noviControl (
  input  [5:0] Ulaz,
  output RegDst,
  output Jump,
  output Branch,
  output MemRead,
  output MemToReg,
  output [1:0] ALUOp,
  output MemWrite,
  output ALUSrc,
  output RegWrite,
  output [1:0] StoreControl,
  output [2:0] LoadControl
);

  wire [15:15] rom_1_data;

  ROM #(.addrWidth(6), .dataWidth(16)) rom_1 (
    .addr(Ulaz),
    .data({rom_1_data[15], RegDst, Jump, Branch, MemRead, MemToReg, ALUOp, MemWrite, ALUSrc, RegWrite, StoreControl, LoadControl}));

  // Notes on the sheet:
  //   contents of rom_1 (hex, n*v repeats v):
  //   4220 4e60 2000 c60 5100 5d60 3100 1d60 8*360 220 4e60 2000 c60 5100 5d60 3100 1d60 60 60 20c0 c0
  //   1140 1140 31c0 11c0 c64 c62 2000 c60 c63 c61 3100 1d60 d0 c8 20c0 c0 1140 1140 31c0 11c0 4220 4e60
  //   2000 c60 5100 5d60 3100 1d60 60 60 20c0 c0 1140 1140 31c0 11c0
endmodule

module InstrukcijskaMemorija (
  input  [31:0] in_1,
  output [31:0] out_2
);

  wire [7:0] undriven, undriven_2, undriven_3, undriven_4, undriven_5, undriven_6, undriven_7, undriven_8,
       undriven_9, undriven_10, undriven_11, undriven_12, undriven_13, undriven_14, undriven_15, undriven_16,
       undriven_17, undriven_18, undriven_19, undriven_20, undriven_21, undriven_22, undriven_23,
       undriven_24, undriven_25, undriven_26, undriven_27, undriven_28, undriven_29, undriven_30,
       undriven_31, undriven_32, undriven_33, undriven_34, undriven_35, undriven_36, undriven_37,
       undriven_38, undriven_39, undriven_40, undriven_41, undriven_42, undriven_43, undriven_44,
       undriven_45, undriven_46, undriven_47, undriven_48, undriven_49, undriven_50, undriven_51,
       undriven_52, undriven_53, undriven_54, undriven_55, undriven_56, undriven_57, undriven_58,
       undriven_59, undriven_60, undriven_61, undriven_62, undriven_63, undriven_64, undriven_65,
       undriven_66, undriven_67, undriven_68, undriven_69, undriven_70, undriven_71, undriven_72,
       undriven_73, undriven_74, undriven_75, undriven_76, undriven_77, undriven_78, undriven_79,
       undriven_80, undriven_81, undriven_82, undriven_83, undriven_84, undriven_85, undriven_86,
       undriven_87, undriven_88, undriven_89, undriven_90, undriven_91, undriven_92, undriven_93,
       undriven_94, undriven_95, undriven_96, undriven_97, undriven_98, undriven_99, undriven_100,
       undriven_101, undriven_102, undriven_103, undriven_104, undriven_105, undriven_106, undriven_107,
       undriven_108, undriven_109, undriven_110, undriven_111, undriven_112, undriven_113, undriven_114,
       undriven_115, undriven_116, undriven_117, undriven_118, undriven_119, undriven_120, undriven_121,
       undriven_122, undriven_123, undriven_124, undriven_125, undriven_126, undriven_127, undriven_128;
  wire [31:0] multiplexer_1_out, multiplexer_2_out, multiplexer_3_out, multiplexer_4_out, multiplexer_5_out,
       multiplexer_6_out, multiplexer_7_out, multiplexer_8_out, multiplexer_9_out, multiplexer_10_out,
       multiplexer_11_out, multiplexer_12_out, multiplexer_13_out, multiplexer_14_out, multiplexer_15_out,
       multiplexer_16_out, multiplexer_17_out, multiplexer_18_out, multiplexer_19_out, multiplexer_20_out,
       multiplexer_21_out, multiplexer_22_out, multiplexer_23_out, multiplexer_24_out, multiplexer_25_out,
       multiplexer_26_out, multiplexer_27_out, multiplexer_28_out, multiplexer_29_out, multiplexer_30_out;

  // ROM #(.addrWidth(24), .line("quad")) rom_1: pin names not known; wires that end beside it: in_1[23:0]
  // ROM #(.addrWidth(24), .line("quad")) rom_2: pin names not known; wires that end beside it: in_1[23:0]
  // ROM #(.addrWidth(24), .line("quad")) rom_3: pin names not known; wires that end beside it: in_1[23:0]
  // ROM #(.addrWidth(24), .line("quad")) rom_4: pin names not known; wires that end beside it: in_1[23:0]
  // ROM #(.addrWidth(24), .line("quad")) rom_5: pin names not known; wires that end beside it: in_1[23:0]
  // ROM #(.addrWidth(24), .line("quad")) rom_6: pin names not known; wires that end beside it: in_1[23:0]
  // ROM #(.addrWidth(24), .line("quad")) rom_7: pin names not known; wires that end beside it: in_1[23:0]
  // ROM #(.addrWidth(24), .line("quad")) rom_8: pin names not known; wires that end beside it: in_1[23:0]
  // ROM #(.addrWidth(24), .line("quad")) rom_9: pin names not known; wires that end beside it: in_1[23:0]
  // ROM #(.addrWidth(24), .line("quad")) rom_10: pin names not known; wires that end beside it: in_1[23:0]
  // ROM #(.addrWidth(24), .line("quad")) rom_11: pin names not known; wires that end beside it: in_1[23:0]
  // ROM #(.addrWidth(24), .line("quad")) rom_12: pin names not known; wires that end beside it: in_1[23:0]
  // ROM #(.addrWidth(24), .line("quad")) rom_13: pin names not known; wires that end beside it: in_1[23:0]
  // ROM #(.addrWidth(24), .line("quad")) rom_14: pin names not known; wires that end beside it: in_1[23:0]
  // ROM #(.addrWidth(24), .line("quad")) rom_15: pin names not known; wires that end beside it: in_1[23:0]
  // ROM #(.addrWidth(24), .line("quad")) rom_16: pin names not known; wires that end beside it: in_1[23:0]
  // ROM #(.addrWidth(24), .line("quad")) rom_17: pin names not known; wires that end beside it: in_1[23:0]
  // ROM #(.addrWidth(24), .line("quad")) rom_18: pin names not known; wires that end beside it: in_1[23:0]
  // ROM #(.addrWidth(24), .line("quad")) rom_19: pin names not known; wires that end beside it: in_1[23:0]
  // ROM #(.addrWidth(24), .line("quad")) rom_20: pin names not known; wires that end beside it: in_1[23:0]
  // ROM #(.addrWidth(24), .line("quad")) rom_21: pin names not known; wires that end beside it: in_1[23:0]
  // ROM #(.addrWidth(24), .line("quad")) rom_22: pin names not known; wires that end beside it: in_1[23:0]
  // ROM #(.addrWidth(24), .line("quad")) rom_23: pin names not known; wires that end beside it: in_1[23:0]
  // ROM #(.addrWidth(24), .line("quad")) rom_24: pin names not known; wires that end beside it: in_1[23:0]
  // ROM #(.addrWidth(24), .line("quad")) rom_25: pin names not known; wires that end beside it: in_1[23:0]
  // ROM #(.addrWidth(24), .line("quad")) rom_26: pin names not known; wires that end beside it: in_1[23:0]
  // ROM #(.addrWidth(24), .line("quad")) rom_27: pin names not known; wires that end beside it: in_1[23:0]
  // ROM #(.addrWidth(24), .line("quad")) rom_28: pin names not known; wires that end beside it: in_1[23:0]
  // ROM #(.addrWidth(24), .line("quad")) rom_29: pin names not known; wires that end beside it: in_1[23:0]
  // ROM #(.addrWidth(24), .line("quad")) rom_30: pin names not known; wires that end beside it: in_1[23:0]
  // ROM #(.addrWidth(24), .line("quad")) rom_31: pin names not known; wires that end beside it: in_1[23:0]
  // ROM #(.addrWidth(24), .line("quad")) rom_32: pin names not known; wires that end beside it: in_1[23:0]
  Multiplexer #(.width(32)) multiplexer_1 (
    .in0({undriven_4, undriven_3, undriven_2, undriven}),
    .in1({undriven_68, undriven_67, undriven_66, undriven_65}), .out(multiplexer_1_out), .sel(in_1[24]));
  Multiplexer #(.width(32)) multiplexer_2 (
    .in0({undriven_8, undriven_7, undriven_6, undriven_5}),
    .in1({undriven_72, undriven_71, undriven_70, undriven_69}), .out(multiplexer_2_out), .sel(in_1[24]));
  Multiplexer #(.width(32)) multiplexer_3 (
    .in0({undriven_12, undriven_11, undriven_10, undriven_9}),
    .in1({undriven_76, undriven_75, undriven_74, undriven_73}), .out(multiplexer_3_out), .sel(in_1[24]));
  Multiplexer #(.width(32)) multiplexer_4 (
    .in0({undriven_16, undriven_15, undriven_14, undriven_13}),
    .in1({undriven_80, undriven_79, undriven_78, undriven_77}), .out(multiplexer_4_out), .sel(in_1[24]));
  Multiplexer #(.width(32)) multiplexer_5 (
    .in0({undriven_20, undriven_19, undriven_18, undriven_17}),
    .in1({undriven_84, undriven_83, undriven_82, undriven_81}), .out(multiplexer_5_out), .sel(in_1[24]));
  Multiplexer #(.width(32)) multiplexer_6 (
    .in0({undriven_24, undriven_23, undriven_22, undriven_21}),
    .in1({undriven_88, undriven_87, undriven_86, undriven_85}), .out(multiplexer_6_out), .sel(in_1[24]));
  Multiplexer #(.width(32)) multiplexer_7 (
    .in0({undriven_28, undriven_27, undriven_26, undriven_25}),
    .in1({undriven_92, undriven_91, undriven_90, undriven_89}), .out(multiplexer_7_out), .sel(in_1[24]));
  Multiplexer #(.width(32)) multiplexer_8 (
    .in0({undriven_32, undriven_31, undriven_30, undriven_29}),
    .in1({undriven_96, undriven_95, undriven_94, undriven_93}), .out(multiplexer_8_out), .sel(in_1[24]));
  Multiplexer #(.width(32)) multiplexer_9 (
    .in0({undriven_36, undriven_35, undriven_34, undriven_33}),
    .in1({undriven_100, undriven_99, undriven_98, undriven_97}), .out(multiplexer_9_out), .sel(in_1[24]));
  Multiplexer #(.width(32)) multiplexer_10 (
    .in0({undriven_40, undriven_39, undriven_38, undriven_37}),
    .in1({undriven_104, undriven_103, undriven_102, undriven_101}), .out(multiplexer_10_out), .sel(in_1[24]));
  Multiplexer #(.width(32)) multiplexer_11 (
    .in0({undriven_44, undriven_43, undriven_42, undriven_41}),
    .in1({undriven_108, undriven_107, undriven_106, undriven_105}), .out(multiplexer_11_out), .sel(in_1[24]));
  Multiplexer #(.width(32)) multiplexer_12 (
    .in0({undriven_48, undriven_47, undriven_46, undriven_45}),
    .in1({undriven_112, undriven_111, undriven_110, undriven_109}), .out(multiplexer_12_out), .sel(in_1[24]));
  Multiplexer #(.width(32)) multiplexer_13 (
    .in0({undriven_52, undriven_51, undriven_50, undriven_49}),
    .in1({undriven_116, undriven_115, undriven_114, undriven_113}), .out(multiplexer_13_out), .sel(in_1[24]));
  Multiplexer #(.width(32)) multiplexer_14 (
    .in0({undriven_56, undriven_55, undriven_54, undriven_53}),
    .in1({undriven_120, undriven_119, undriven_118, undriven_117}), .out(multiplexer_14_out), .sel(in_1[24]));
  Multiplexer #(.width(32)) multiplexer_15 (
    .in0({undriven_60, undriven_59, undriven_58, undriven_57}),
    .in1({undriven_124, undriven_123, undriven_122, undriven_121}), .out(multiplexer_15_out), .sel(in_1[24]));
  Multiplexer #(.width(32)) multiplexer_16 (
    .in0({undriven_64, undriven_63, undriven_62, undriven_61}),
    .in1({undriven_128, undriven_127, undriven_126, undriven_125}), .out(multiplexer_16_out), .sel(in_1[24]));
  Multiplexer #(.width(32)) multiplexer_17 (
    .in0(multiplexer_1_out), .in1(multiplexer_2_out), .out(multiplexer_17_out), .sel(in_1[25]));
  Multiplexer #(.width(32)) multiplexer_18 (
    .in0(multiplexer_3_out), .in1(multiplexer_4_out), .out(multiplexer_18_out), .sel(in_1[25]));
  Multiplexer #(.width(32)) multiplexer_19 (
    .in0(multiplexer_5_out), .in1(multiplexer_6_out), .out(multiplexer_19_out), .sel(in_1[25]));
  Multiplexer #(.width(32)) multiplexer_20 (
    .in0(multiplexer_7_out), .in1(multiplexer_8_out), .out(multiplexer_20_out), .sel(in_1[25]));
  Multiplexer #(.width(32)) multiplexer_21 (
    .in0(multiplexer_9_out), .in1(multiplexer_10_out), .out(multiplexer_21_out), .sel(in_1[25]));
  Multiplexer #(.width(32)) multiplexer_22 (
    .in0(multiplexer_11_out), .in1(multiplexer_12_out), .out(multiplexer_22_out), .sel(in_1[25]));
  Multiplexer #(.width(32)) multiplexer_23 (
    .in0(multiplexer_13_out), .in1(multiplexer_14_out), .out(multiplexer_23_out), .sel(in_1[25]));
  Multiplexer #(.width(32)) multiplexer_24 (
    .in0(multiplexer_15_out), .in1(multiplexer_16_out), .out(multiplexer_24_out), .sel(in_1[25]));
  Multiplexer #(.width(32)) multiplexer_25 (
    .in0(multiplexer_17_out), .in1(multiplexer_18_out), .out(multiplexer_25_out), .sel(in_1[26]));
  Multiplexer #(.width(32)) multiplexer_26 (
    .in0(multiplexer_19_out), .in1(multiplexer_20_out), .out(multiplexer_26_out), .sel(in_1[26]));
  Multiplexer #(.width(32)) multiplexer_27 (
    .in0(multiplexer_21_out), .in1(multiplexer_22_out), .out(multiplexer_27_out), .sel(in_1[26]));
  Multiplexer #(.width(32)) multiplexer_28 (
    .in0(multiplexer_23_out), .in1(multiplexer_24_out), .out(multiplexer_28_out), .sel(in_1[26]));
  Multiplexer #(.width(32)) multiplexer_29 (
    .in0(multiplexer_25_out), .in1(multiplexer_26_out), .out(multiplexer_29_out), .sel(in_1[27]));
  Multiplexer #(.width(32)) multiplexer_30 (
    .in0(multiplexer_27_out), .in1(multiplexer_28_out), .out(multiplexer_30_out), .sel(in_1[27]));
  Multiplexer #(.width(32)) multiplexer_31 (
    .in0(multiplexer_29_out), .in1(multiplexer_30_out), .out(out_2), .sel(in_1[28]));

  // Other names for the same wires on the sheet: bit23do0[23:0] = in_1[23:0]; bit24 = in_1[24]; bit25 = in_1[25];
  //   bit26 = in_1[26]; bit27 = in_1[27]; bit28 = in_1[28]

  // Notes on the sheet:
  //   contents of rom_1 (hex, n*v repeats v):
  //   21 8 7f ff 21 29 ff ff 1 9 40 22
  //   contents of rom_2 (hex, n*v repeats v):
  //   21 8 7f ff 21 29 7f ff 1 9 40 22
endmodule

module EQ1bit (
  input  A,
  input  B,
  output EQ
);

  wire xor_1_out;

  xor xor_1 (xor_1_out, A, B);
  not not_1 (EQ, xor_1_out);
endmodule

module EQ4bit (
  input  [3:0] A,
  input  [3:0] B,
  output Izlaz
);

  wire eq1bit_1_eq, eq1bit_2_eq, eq1bit_3_eq, eq1bit_4_eq;

  EQ1bit eq1bit_1 (.A(A[3]), .B(B[3]), .EQ(eq1bit_1_eq));
  EQ1bit eq1bit_2 (.A(A[2]), .B(B[2]), .EQ(eq1bit_2_eq));
  EQ1bit eq1bit_3 (.A(A[1]), .B(B[1]), .EQ(eq1bit_3_eq));
  EQ1bit eq1bit_4 (.A(A[0]), .B(B[0]), .EQ(eq1bit_4_eq));
  and and_1 (Izlaz, eq1bit_4_eq, eq1bit_2_eq, eq1bit_1_eq);
endmodule

module EQ5bit (
  input  [4:0] A,
  input  [4:0] B,
  output Izlaz
);

  wire eq1bit_1_eq, eq1bit_2_eq, eq1bit_3_eq, eq1bit_4_eq, eq1bit_5_eq;

  EQ1bit eq1bit_1 (.A(A[0]), .B(B[0]), .EQ(eq1bit_1_eq));
  EQ1bit eq1bit_2 (.A(A[1]), .B(B[1]), .EQ(eq1bit_2_eq));
  EQ1bit eq1bit_3 (.A(A[2]), .B(B[2]), .EQ(eq1bit_3_eq));
  EQ1bit eq1bit_4 (.A(A[3]), .B(B[3]), .EQ(eq1bit_4_eq));
  EQ1bit eq1bit_5 (.A(A[4]), .B(B[4]), .EQ(eq1bit_5_eq));
  and and_1 (Izlaz, eq1bit_5_eq, eq1bit_4_eq, eq1bit_3_eq, eq1bit_2_eq, eq1bit_1_eq);
endmodule

module EQ8bit (
  input  [7:0] A,
  input  [7:0] B,
  output Izlaz
);

  wire eq1bit_1_eq, eq1bit_2_eq, eq1bit_3_eq, eq1bit_4_eq, eq1bit_5_eq, eq1bit_6_eq, eq1bit_7_eq, eq1bit_8_eq;

  EQ1bit eq1bit_1 (.A(A[7]), .B(B[7]), .EQ(eq1bit_1_eq));
  EQ1bit eq1bit_2 (.A(A[6]), .B(B[6]), .EQ(eq1bit_2_eq));
  EQ1bit eq1bit_3 (.A(A[5]), .B(B[5]), .EQ(eq1bit_3_eq));
  EQ1bit eq1bit_4 (.A(A[4]), .B(B[4]), .EQ(eq1bit_4_eq));
  EQ1bit eq1bit_5 (.A(A[3]), .B(B[3]), .EQ(eq1bit_5_eq));
  and and_1 (Izlaz, eq1bit_1_eq, eq1bit_2_eq, eq1bit_3_eq, eq1bit_4_eq, eq1bit_5_eq, eq1bit_6_eq, eq1bit_7_eq, eq1bit_8_eq);
  EQ1bit eq1bit_6 (.A(A[2]), .B(B[2]), .EQ(eq1bit_6_eq));
  EQ1bit eq1bit_7 (.A(A[1]), .B(B[1]), .EQ(eq1bit_7_eq));
  EQ1bit eq1bit_8 (.A(A[0]), .B(B[0]), .EQ(eq1bit_8_eq));
endmodule

module EQ32bit (
  input  [31:0] A,
  input  [31:0] B,
  output EQ
);

  wire eq8bit_1_izlaz, eq8bit_2_izlaz, eq8bit_3_izlaz, eq8bit_4_izlaz;

  EQ8bit eq8bit_1 (.A(A[31:24]), .B(B[31:24]), .Izlaz(eq8bit_1_izlaz));
  EQ8bit eq8bit_2 (.A(A[23:16]), .B(B[23:16]), .Izlaz(eq8bit_2_izlaz));
  and and_1 (EQ, eq8bit_1_izlaz, eq8bit_2_izlaz, eq8bit_3_izlaz, eq8bit_4_izlaz);
  EQ8bit eq8bit_3 (.A(A[15:8]), .B(B[15:8]), .Izlaz(eq8bit_3_izlaz));
  EQ8bit eq8bit_4 (.A(A[7:0]), .B(B[7:0]), .Izlaz(eq8bit_4_izlaz));
endmodule

module JedinicaZaProsljedjivanje (
  input  MEMRegWrite,
  input  WBRegWrite,
  input  [4:0] RdMEM,
  input  [4:0] Rs,
  input  [4:0] RdWB,
  input  [4:0] Rt,
  input  [4:0] RsID,
  input  [4:0] RtID,
  output [1:0] ForwardA,
  output [1:0] ForwardB,
  output [1:0] ForwardBranch1,
  output [1:0] ForwardBranch2
);

  wire eq5bit_5_izlaz, eq5bit_6_izlaz, MEM_0, MEM_A, MEM_A_ID, MEM_B, MEM_B_ID, WB_0, WB_A, WB_A_ID, WB_B,
       WB_B_ID;
  wire [1:0] and_1_out, and_3_out, and_5_out, and_7_out;

  EQ5bit eq5bit_1 (.A(RdMEM), .B(Rs), .Izlaz(MEM_A));
  EQ5bit eq5bit_2 (.A(RdWB), .B(Rs), .Izlaz(WB_A));
  EQ5bit eq5bit_3 (.A(RdMEM), .B(Rt), .Izlaz(MEM_B));
  EQ5bit eq5bit_4 (.A(RdWB), .B(Rt), .Izlaz(WB_B));
  EQ5bit eq5bit_5 (.A(RdMEM), .B({5{1'b0}}), .Izlaz(eq5bit_5_izlaz));
  EQ5bit eq5bit_6 (.A(RdWB), .B({5{1'b0}}), .Izlaz(eq5bit_6_izlaz));
  EQ5bit eq5bit_7 (.A(RdMEM), .B(RsID), .Izlaz(MEM_A_ID));
  EQ5bit eq5bit_8 (.A(RdWB), .B(RsID), .Izlaz(WB_A_ID));
  EQ5bit eq5bit_9 (.A(RdMEM), .B(RtID), .Izlaz(MEM_B_ID));
  EQ5bit eq5bit_10 (.A(RdWB), .B(RtID), .Izlaz(WB_B_ID));
  not not_1 (MEM_0, eq5bit_5_izlaz);
  not not_2 (WB_0, eq5bit_6_izlaz);
  and and_1 (and_1_out[0], MEM_A, MEMRegWrite, MEM_0);
  and and_2 (and_1_out[1], WB_A, WBRegWrite, WB_0);
  and and_3 (and_3_out[0], MEM_B, MEMRegWrite, MEM_0);
  and and_4 (and_3_out[1], WB_B, WBRegWrite, WB_0);
  and and_5 (and_5_out[0], MEM_A_ID, MEMRegWrite, MEM_0);
  and and_6 (and_5_out[1], WB_A_ID, WBRegWrite, WB_0);
  and and_7 (and_7_out[0], MEM_B_ID, MEMRegWrite, MEM_0);
  and and_8 (and_7_out[1], WB_B_ID, WBRegWrite, WB_0);
  Multiplexer #(.select(2), .width(2)) multiplexer_1 (
    .in0(and_1_out), .in1(and_1_out), .in2(and_1_out), .in3(2'b01), .out(ForwardA), .sel(and_1_out));
  Multiplexer #(.select(2), .width(2)) multiplexer_2 (
    .in0(and_3_out), .in1(and_3_out), .in2(and_3_out), .in3(2'b01), .out(ForwardB), .sel(and_3_out));
  Multiplexer #(.select(2), .width(2)) multiplexer_3 (
    .in0(and_5_out), .in1(and_5_out), .in2(and_5_out), .in3(2'b01), .out(ForwardBranch1), .sel(and_5_out));
  Multiplexer #(.select(2), .width(2)) multiplexer_4 (
    .in0(and_7_out), .in1(and_7_out), .in2(and_7_out), .in3(2'b01), .out(ForwardBranch2), .sel(and_7_out));

  // Other names for the same wires on the sheet: MEMWrite = MEMRegWrite; WBWrite = WBRegWrite

  // Notes on the sheet:
  //   00 Nema prosljedjivanja
  //   01 Prosljedjivanje sa MEM
  //   10 Prosljedjivanje sa WB
endmodule

module SLL32bit (
  input  [31:0] Ulaz,
  input  [4:0] Ctrl,
  output [31:0] Izlaz
);

  wire [31:0] Ls11_t;

  Multiplexer #(.select(5), .width(32)) multiplexer_1 (
    .in0(Ulaz), .in1({Ulaz[30:0], 1'b0}), .in2({Ulaz[29:0], 2'b00}), .in3({Ulaz[28:0], 3'b000}),
    .in4({Ulaz[27:0], 4'b0000}), .in5({Ulaz[26:0], {5{1'b0}}}), .in6({Ulaz[25:0], {6{1'b0}}}),
    .in7({Ulaz[24:0], {7{1'b0}}}), .in8({Ulaz[23:0], {8{1'b0}}}), .in9({Ulaz[22:0], {9{1'b0}}}),
    .in10({Ulaz[21:0], {10{1'b0}}}), .in11(Ls11_t), .in12({Ulaz[19:0], {12{1'b0}}}),
    .in13({Ulaz[18:0], {13{1'b0}}}), .in14({Ulaz[17:0], {14{1'b0}}}), .in15({Ulaz[16:0], {15{1'b0}}}),
    .in16({Ulaz[15:0], {16{1'b0}}}), .in17({Ulaz[14:0], {17{1'b0}}}), .in18({Ulaz[13:0], {18{1'b0}}}),
    .in19({Ulaz[12:0], {19{1'b0}}}), .in20({Ulaz[11:0], {20{1'b0}}}), .in21({Ulaz[10:0], {21{1'b0}}}),
    .in22({Ulaz[9:0], {22{1'b0}}}), .in23({Ulaz[8:0], {23{1'b0}}}), .in24({Ulaz[7:0], {24{1'b0}}}),
    .in25({Ulaz[6:0], {25{1'b0}}}), .in26({Ulaz[5:0], {26{1'b0}}}), .in27({Ulaz[4:0], {27{1'b0}}}),
    .in28({Ulaz[3:0], {28{1'b0}}}), .in29({Ulaz[2:0], {29{1'b0}}}), .in30({Ulaz[1:0], {30{1'b0}}}),
    .in31({Ulaz[0], {31{1'b0}}}), .out(Izlaz), .sel(Ctrl));

  // Other names for the same wires on the sheet: LS1[31:1] = Ulaz[30:0]; LS2[31:2] = Ulaz[29:0];
  //   LS3[31:3] = Ulaz[28:0]; LS4[31:4] = Ulaz[27:0]; LS5[31:5] = Ulaz[26:0]; LS6[31:6] = Ulaz[25:0];
  //   LS7[31:7] = Ulaz[24:0]; LS8[31:8] = Ulaz[23:0]; LS9[31:9] = Ulaz[22:0]; LS10[31:10] = Ulaz[21:0];
  //   LS11[31:11] = Ulaz[20:0]; LS12[31:12] = Ulaz[19:0]; LS13[31:13] = Ulaz[18:0]; LS14[31:14] = Ulaz[17:0];
  //   LS15[31:15] = Ulaz[16:0]; LS16[31:16] = Ulaz[15:0]; LS17[31:17] = Ulaz[14:0]; LS18[31:18] = Ulaz[13:0];
  //   LS19[31:19] = Ulaz[12:0]; LS20[31:20] = Ulaz[11:0]; LS21[31:21] = Ulaz[10:0]; LS22[31:22] = Ulaz[9:0];
  //   LS23[31:23] = Ulaz[8:0]; LS24[31:24] = Ulaz[7:0]; LS25[31:25] = Ulaz[6:0]; LS26[31:26] = Ulaz[5:0];
  //   LS27[31:27] = Ulaz[4:0]; LS28[31:28] = Ulaz[3:0]; LS29[31:29] = Ulaz[2:0]; LS30[31:30] = Ulaz[1:0];
  //   LS31[31] = Ulaz[0]
endmodule

module SRL32bit (
  input  [31:0] Ulaz,
  input  [4:0] Ctrl,
  output [31:0] Izlaz
);

  Multiplexer #(.select(5), .width(32)) multiplexer_1 (
    .in0(Ulaz), .in1({1'b0, Ulaz[31:1]}), .in2({2'b00, Ulaz[31:2]}), .in3({3'b000, Ulaz[31:3]}),
    .in4({4'b0000, Ulaz[31:4]}), .in5({{5{1'b0}}, Ulaz[31:5]}), .in6({{6{1'b0}}, Ulaz[31:6]}),
    .in7({{7{1'b0}}, Ulaz[31:7]}), .in8({{8{1'b0}}, Ulaz[31:8]}), .in9({{9{1'b0}}, Ulaz[31:9]}),
    .in10({{10{1'b0}}, Ulaz[31:10]}), .in11({{11{1'b0}}, Ulaz[31:11]}), .in12({{12{1'b0}}, Ulaz[31:12]}),
    .in13({{13{1'b0}}, Ulaz[31:13]}), .in14({{14{1'b0}}, Ulaz[31:14]}), .in15({{15{1'b0}}, Ulaz[31:15]}),
    .in16({{16{1'b0}}, Ulaz[31:16]}), .in17({{17{1'b0}}, Ulaz[31:17]}), .in18({{18{1'b0}}, Ulaz[31:18]}),
    .in19({{19{1'b0}}, Ulaz[31:19]}), .in20({{20{1'b0}}, Ulaz[31:20]}), .in21({{21{1'b0}}, Ulaz[31:21]}),
    .in22({{22{1'b0}}, Ulaz[31:22]}), .in23({{23{1'b0}}, Ulaz[31:23]}), .in24({{24{1'b0}}, Ulaz[31:24]}),
    .in25({{25{1'b0}}, Ulaz[31:25]}), .in26({{26{1'b0}}, Ulaz[31:26]}), .in27({{27{1'b0}}, Ulaz[31:27]}),
    .in28({{28{1'b0}}, Ulaz[31:28]}), .in29({{29{1'b0}}, Ulaz[31:29]}), .in30({{30{1'b0}}, Ulaz[31:30]}),
    .in31({{31{1'b0}}, Ulaz[31]}), .out(Izlaz), .sel(Ctrl));

  // Other names for the same wires on the sheet: RS1[30:0] = Ulaz[31:1]; RS2[29:0] = Ulaz[31:2];
  //   RS3[28:0] = Ulaz[31:3]; RS4[27:0] = Ulaz[31:4]; RS5[26:0] = Ulaz[31:5]; RS6[25:0] = Ulaz[31:6];
  //   RS7[24:0] = Ulaz[31:7]; RS8[23:0] = Ulaz[31:8]; RS9[22:0] = Ulaz[31:9]; RS10[21:0] = Ulaz[31:10];
  //   RS11[20:0] = Ulaz[31:11]; RS12[19:0] = Ulaz[31:12]; RS13[18:0] = Ulaz[31:13]; RS14[17:0] = Ulaz[31:14];
  //   RS15[16:0] = Ulaz[31:15]; RS16[15:0] = Ulaz[31:16]; RS17[14:0] = Ulaz[31:17]; RS18[13:0] = Ulaz[31:18];
  //   RS19[12:0] = Ulaz[31:19]; RS20[11:0] = Ulaz[31:20]; RS21[10:0] = Ulaz[31:21]; RS22[9:0] = Ulaz[31:22];
  //   RS23[8:0] = Ulaz[31:23]; RS24[7:0] = Ulaz[31:24]; RS25[6:0] = Ulaz[31:25]; RS26[5:0] = Ulaz[31:26];
  //   RS27[4:0] = Ulaz[31:27]; RS28[3:0] = Ulaz[31:28]; RS29[2:0] = Ulaz[31:29]; RS30[1:0] = Ulaz[31:30];
  //   RS31[0] = Ulaz[31]
endmodule

module SRA32 (
  input  [31:0] Ulaz,
  input  [4:0] Ctrl,
  output [31:0] Izlaz
);

  wire [31:1] RS31;
  wire [31:2] RS30;
  wire [31:3] RS29;
  wire [31:4] RS28;
  wire [31:5] RS27;
  wire [31:6] RS26;
  wire [31:7] RS25;
  wire [31:8] RS24;
  wire [31:9] RS23;
  wire [31:10] RS22;
  wire [31:11] RS21;
  wire [31:12] RS20;
  wire [31:13] RS19;
  wire [31:14] RS18;
  wire [31:15] RS17;
  wire [31:16] RS16;
  wire [31:17] RS15;
  wire [31:18] RS14;
  wire [31:19] RS13;
  wire [31:20] RS12;
  wire [31:21] RS11;
  wire [31:22] RS10;
  wire [31:23] RS9;
  wire [31:24] RS8;
  wire [31:25] RS7;
  wire [31:26] RS6;
  wire [31:27] RS5;
  wire [31:28] RS4;
  wire [31:29] RS3;
  wire [31:30] RS2;
  wire [31:31] RS1;

  Multiplexer #(.width(31)) multiplexer_1 (.in0({31{1'b0}}), .in1({31{1'b1}}), .out(RS31), .sel(Ulaz[31]));
  Multiplexer #(.width(30)) multiplexer_2 (.in0({30{1'b0}}), .in1({30{1'b1}}), .out(RS30), .sel(Ulaz[31]));
  Multiplexer #(.width(29)) multiplexer_3 (.in0({29{1'b0}}), .in1({29{1'b1}}), .out(RS29), .sel(Ulaz[31]));
  Multiplexer #(.width(28)) multiplexer_4 (.in0({28{1'b0}}), .in1({28{1'b1}}), .out(RS28), .sel(Ulaz[31]));
  Multiplexer #(.width(27)) multiplexer_5 (.in0({27{1'b0}}), .in1({27{1'b1}}), .out(RS27), .sel(Ulaz[31]));
  Multiplexer #(.width(26)) multiplexer_6 (.in0({26{1'b0}}), .in1({26{1'b1}}), .out(RS26), .sel(Ulaz[31]));
  Multiplexer #(.width(25)) multiplexer_7 (.in0({25{1'b0}}), .in1({25{1'b1}}), .out(RS25), .sel(Ulaz[31]));
  Multiplexer #(.width(24)) multiplexer_8 (.in0({24{1'b0}}), .in1({24{1'b1}}), .out(RS24), .sel(Ulaz[31]));
  Multiplexer #(.width(23)) multiplexer_9 (.in0({23{1'b0}}), .in1({23{1'b1}}), .out(RS23), .sel(Ulaz[31]));
  Multiplexer #(.width(22)) multiplexer_10 (.in0({22{1'b0}}), .in1({22{1'b1}}), .out(RS22), .sel(Ulaz[31]));
  Multiplexer #(.width(21)) multiplexer_11 (.in0({21{1'b0}}), .in1({21{1'b1}}), .out(RS21), .sel(Ulaz[31]));
  Multiplexer #(.width(20)) multiplexer_12 (.in0({20{1'b0}}), .in1({20{1'b1}}), .out(RS20), .sel(Ulaz[31]));
  Multiplexer #(.width(19)) multiplexer_13 (.in0({19{1'b0}}), .in1({19{1'b1}}), .out(RS19), .sel(Ulaz[31]));
  Multiplexer #(.width(18)) multiplexer_14 (.in0({18{1'b0}}), .in1({18{1'b1}}), .out(RS18), .sel(Ulaz[31]));
  Multiplexer #(.width(17)) multiplexer_15 (.in0({17{1'b0}}), .in1({17{1'b1}}), .out(RS17), .sel(Ulaz[31]));
  Multiplexer #(.width(16)) multiplexer_16 (.in0({16{1'b0}}), .in1({16{1'b1}}), .out(RS16), .sel(Ulaz[31]));
  Multiplexer #(.width(15)) multiplexer_17 (.in0({15{1'b0}}), .in1({15{1'b1}}), .out(RS15), .sel(Ulaz[31]));
  Multiplexer #(.width(14)) multiplexer_18 (.in0({14{1'b0}}), .in1({14{1'b1}}), .out(RS14), .sel(Ulaz[31]));
  Multiplexer #(.width(13)) multiplexer_19 (.in0({13{1'b0}}), .in1({13{1'b1}}), .out(RS13), .sel(Ulaz[31]));
  Multiplexer #(.width(12)) multiplexer_20 (.in0({12{1'b0}}), .in1({12{1'b1}}), .out(RS12), .sel(Ulaz[31]));
  Multiplexer #(.width(11)) multiplexer_21 (.in0({11{1'b0}}), .in1({11{1'b1}}), .out(RS11), .sel(Ulaz[31]));
  Multiplexer #(.width(10)) multiplexer_22 (.in0({10{1'b0}}), .in1({10{1'b1}}), .out(RS10), .sel(Ulaz[31]));
  Multiplexer #(.width(9)) multiplexer_23 (.in0({9{1'b0}}), .in1({9{1'b1}}), .out(RS9), .sel(Ulaz[31]));
  Multiplexer #(.width(8)) multiplexer_24 (.in0({8{1'b0}}), .in1({8{1'b1}}), .out(RS8), .sel(Ulaz[31]));
  Multiplexer #(.width(7)) multiplexer_25 (.in0({7{1'b0}}), .in1({7{1'b1}}), .out(RS7), .sel(Ulaz[31]));
  Multiplexer #(.width(6)) multiplexer_26 (.in0({6{1'b0}}), .in1({6{1'b1}}), .out(RS6), .sel(Ulaz[31]));
  Multiplexer #(.width(5)) multiplexer_27 (.in0({5{1'b0}}), .in1({5{1'b1}}), .out(RS5), .sel(Ulaz[31]));
  Multiplexer #(.width(4)) multiplexer_28 (.in0(4'b0000), .in1(4'b1111), .out(RS4), .sel(Ulaz[31]));
  Multiplexer #(.width(3)) multiplexer_29 (.in0(3'b000), .in1(3'b111), .out(RS3), .sel(Ulaz[31]));
  Multiplexer #(.width(2)) multiplexer_30 (.in0(2'b00), .in1(2'b11), .out(RS2), .sel(Ulaz[31]));
  Multiplexer multiplexer_31 (.in0(1'b0), .in1(1'b1), .out(RS1[31]), .sel(Ulaz[31]));
  Multiplexer #(.select(5), .width(32)) multiplexer_32 (
    .in0(Ulaz), .in1({RS1[31], Ulaz[31:1]}), .in2({RS2, Ulaz[31:2]}), .in3({RS3, Ulaz[31:3]}),
    .in4({RS4, Ulaz[31:4]}), .in5({RS5, Ulaz[31:5]}), .in6({RS6, Ulaz[31:6]}), .in7({RS7, Ulaz[31:7]}),
    .in8({RS8, Ulaz[31:8]}), .in9({RS9, Ulaz[31:9]}), .in10({RS10, Ulaz[31:10]}), .in11({RS11, Ulaz[31:11]}),
    .in12({RS12, Ulaz[31:12]}), .in13({RS13, Ulaz[31:13]}), .in14({RS14, Ulaz[31:14]}),
    .in15({RS15, Ulaz[31:15]}), .in16({RS16, Ulaz[31:16]}), .in17({RS17, Ulaz[31:17]}),
    .in18({RS18, Ulaz[31:18]}), .in19({RS19, Ulaz[31:19]}), .in20({RS20, Ulaz[31:20]}),
    .in21({RS21, Ulaz[31:21]}), .in22({RS22, Ulaz[31:22]}), .in23({RS23, Ulaz[31:23]}),
    .in24({RS24, Ulaz[31:24]}), .in25({RS25, Ulaz[31:25]}), .in26({RS26, Ulaz[31:26]}),
    .in27({RS27, Ulaz[31:27]}), .in28({RS28, Ulaz[31:28]}), .in29({RS29, Ulaz[31:29]}),
    .in30({RS30, Ulaz[31:30]}), .in31({RS31, Ulaz[31]}), .out(Izlaz), .sel(Ctrl));

  // Other names for the same wires on the sheet: RS1[30:0] = Ulaz[31:1]; RS2[29:0] = Ulaz[31:2];
  //   RS3[28:0] = Ulaz[31:3]; RS4[27:0] = Ulaz[31:4]; RS5[26:0] = Ulaz[31:5]; RS6[25:0] = Ulaz[31:6];
  //   RS7[24:0] = Ulaz[31:7]; RS8[23:0] = Ulaz[31:8]; RS9[22:0] = Ulaz[31:9]; RS10[21:0] = Ulaz[31:10];
  //   RS11[20:0] = Ulaz[31:11]; RS12[19:0] = Ulaz[31:12]; RS13[18:0] = Ulaz[31:13]; RS14[17:0] = Ulaz[31:14];
  //   RS15[16:0] = Ulaz[31:15]; RS16[15:0] = Ulaz[31:16]; RS17[14:0] = Ulaz[31:17]; RS18[13:0] = Ulaz[31:18];
  //   RS19[12:0] = Ulaz[31:19]; RS20[11:0] = Ulaz[31:20]; RS21[10:0] = Ulaz[31:21]; RS22[9:0] = Ulaz[31:22];
  //   RS23[8:0] = Ulaz[31:23]; RS24[7:0] = Ulaz[31:24]; RS25[6:0] = Ulaz[31:25]; RS26[5:0] = Ulaz[31:26];
  //   RS27[4:0] = Ulaz[31:27]; RS28[3:0] = Ulaz[31:28]; RS29[2:0] = Ulaz[31:29]; RS30[1:0] = Ulaz[31:30];
  //   Bit1 = Ulaz[31]; RS31[0] = Ulaz[31]
endmodule

module JedinicaZaDetekcijuHazarda (
  input  [4:0] IFIDRs,
  input  [4:0] IFIDRt,
  input  MemReadEx,
  input  [4:0] EXWriteReg,
  input  IDBranch,
  input  EXRegWrite,
  input  MEMMemRead,
  input  [4:0] MEMWriteReg,
  input  JumpReg,
  output PCWrite,
  output IFIDWrite,
  output MuxControl
);

  wire and_1_out, and_2_out, and_3_out, MEMRs, MEMRt, or_1_out, or_2_out, or_3_out, or_4_out, RsRt, RtRt;

  EQ5bit eq5bit_1 (.A(IFIDRs), .B(EXWriteReg), .Izlaz(RsRt));
  EQ5bit eq5bit_2 (.A(IFIDRt), .B(EXWriteReg), .Izlaz(RtRt));
  EQ5bit eq5bit_3 (.A(IFIDRs), .B(MEMWriteReg), .Izlaz(MEMRs));
  EQ5bit eq5bit_4 (.A(IFIDRt), .B(MEMWriteReg), .Izlaz(MEMRt));
  or or_1 (or_1_out, RsRt, RtRt);
  or or_2 (or_2_out, JumpReg, IDBranch);
  or or_3 (or_3_out, MEMRs, MEMRt);
  or or_4 (or_4_out, IDBranch, JumpReg);
  and and_1 (and_1_out, MemReadEx, or_1_out);
  and and_2 (and_2_out, or_1_out, or_2_out, EXRegWrite);
  and and_3 (and_3_out, or_3_out, or_4_out, MEMMemRead);
  or or_5 (MuxControl, and_1_out, and_2_out, and_3_out);
  not not_1 (IFIDWrite, MuxControl);
  not not_2 (PCWrite, MuxControl);

  // Other names for the same wires on the sheet: JR = JumpReg; MemRead = MemReadEx; Mux = MuxControl;
  //   Rs[4:0] = IFIDRs; Rt1[4:0] = IFIDRt; Rt2[4:0] = EXWriteReg
endmodule

module StoreControl (
  input  [1:0] StoreOp,
  input  [31:0] DI,
  output [3:0] LE,
  output [31:0] DO
);

  Multiplexer #(.select(2), .width(4)) multiplexer_1 (
    .in0(4'b1111), .in1(4'b0011), .in2(4'b0001), .out(LE), .sel(StoreOp));  // open: in3
  Multiplexer #(.select(2), .width(32)) multiplexer_2 (
    .in0(DI), .in1({DI[15:0], {16{1'b0}}}), .in2({DI[7:0], {24{1'b0}}}), .out(DO), .sel(StoreOp));  // open: in3

  // Notes on the sheet:
  //   0 - sw
  //   1 - sh
  //   2 - sb
endmodule

module LoadControl (
  input  OE,
  input  [2:0] LoadOp,
  input  [31:0] DI,
  output [31:0] DO
);

  wire [31:0] multiplexer_1_out;

  Multiplexer #(.select(3), .width(32)) multiplexer_1 (
    .in0(DI), .in1({{16{1'b0}}, DI[31:16]}), .in2({{17{DI[31]}}, DI[30:16]}), .in3({{24{1'b0}}, DI[31:24]}),
    .in4({{25{DI[31]}}, DI[30:24]}), .out(multiplexer_1_out), .sel(LoadOp));  // open: in5, in6, in7
  Multiplexer #(.width(32)) multiplexer_2 (.in0({32{1'b0}}), .in1(multiplexer_1_out), .out(DO), .sel(OE));

  // Other names for the same wires on the sheet: LO[2:0] = LoadOp

  // Notes on the sheet:
  //   0 - lw
  //   1 - lhu
  //   2 - lh
  //   3 - lbu
  //   4 - lb
endmodule

module ZadrskaJDH (
  input  PCWriteI,
  input  IFIDWriteI,
  input  CLK,
  input  RST,
  output PCWrite,
  output IFIDWrite
);

  wire not_1_out;

  not not_1 (not_1_out, CLK);
  D_Flip_Flop d_ff_1 (.D(PCWriteI), .clk(not_1_out), .Q(PCWrite), .reset(RST));  // open: Qn, preset
  D_Flip_Flop d_ff_2 (.D(IFIDWriteI), .clk(not_1_out), .Q(IFIDWrite), .reset(RST));  // open: Qn, preset
endmodule

module JedinicaZaDetekcijuGrananja (
  input  [31:0] ReadData1,
  input  [31:0] ReadData2,
  input  [5:0] Opcode,
  input  [4:0] ReadReg2,
  output Branch,
  output Link
);

  wire and_1_out, and_2_out, BgBl, Jednako0, JednakoD2, Manje0, ManjeD2, ManjeJednako0, multiplexer_2_out,
       not_1_out, not_2_out, not_3_out, not_4_out, not_5_out, not_6_out, not_7_out, not_8_out, Razlicito0,
       RazlicitoD2, Vece0, VeceJednako0, VeceJednakoD2;
  wire [2:0] not_13_out;

  not not_1 (not_1_out, Opcode[5]);
  not not_2 (not_2_out, Opcode[4]);
  not not_3 (not_3_out, Opcode[3]);
  not not_4 (not_4_out, Opcode[2]);
  not not_5 (not_5_out, Opcode[1]);
  not not_6 (not_6_out, ReadReg2[3]);
  not not_7 (not_7_out, ReadReg2[2]);
  not not_8 (not_8_out, ReadReg2[1]);
  EQ32bit eq32bit_1 (.A(ReadData1), .B(ReadData2), .EQ(JednakoD2));
  EQ32bit eq32bit_2 (.A(ReadData1), .B({32{1'b0}}), .EQ(Jednako0));
  SLT32b slt32b_1 (.A(ReadData1), .B(ReadData2), .SLT(ManjeD2));
  SLT32b slt32b_2 (.A(ReadData1), .B({32{1'b0}}), .SLT(Manje0));
  not not_9 (RazlicitoD2, JednakoD2);
  not not_10 (Razlicito0, Jednako0);
  not not_11 (VeceJednakoD2, ManjeD2);
  not not_12 (VeceJednako0, Manje0);
  and and_1 (and_1_out, not_1_out, not_2_out, not_3_out, not_4_out, not_5_out, Opcode[0]);
  and and_2 (and_2_out, ReadReg2[4], not_6_out, not_7_out, not_8_out);
  and and_3 (Link, and_1_out, and_2_out);
  and and_4 (Vece0, VeceJednako0, Razlicito0);
  or or_1 (ManjeJednako0, Manje0, Jednako0);
  Multiplexer #(.select(2)) multiplexer_1 (
    .in0(ManjeD2), .in1(VeceJednako0), .in2(ManjeD2), .in3(VeceJednako0), .out(BgBl),
    .sel({ReadReg2[4], ReadReg2[0]}));
  Multiplexer #(.select(3)) multiplexer_2 (
    .in0(1'b0), .in1(BgBl), .in2(1'b0), .in3(1'b0), .in4(JednakoD2), .in5(RazlicitoD2), .in6(ManjeJednako0),
    .in7(Vece0), .out(multiplexer_2_out), .sel(Opcode[2:0]));
  assign not_13_out = ~Opcode[5:3];  // NOT_Gate not_13, 3 bits wide
  and and_5 (Branch, multiplexer_2_out, not_13_out[0], not_13_out[1], not_13_out[2]);

  // Other names for the same wires on the sheet: Data1[31:0] = ReadData1; Data2[31:0] = ReadData2;
  //   Kontrol1[2:0] = Opcode[2:0]; Op3bit[2:0] = Opcode[5:3]; Kontrol2[1:0] = {ReadReg2[4], ReadReg2[0]};
  //   Reg2[4:0] = ReadReg2
endmodule

module JedinicaZaDetekcijuSkokova (
  input  [5:0] Op,
  input  [5:0] Instr,
  output Jump,
  output JR,
  output Link,
  output LinkReg
);

  wire J, JAL, JR_t, nor_3_out, nor_4_out, nor_5_out, not_1_out, not_2_out, not_3_out, not_4_out, not_5_out,
       not_6_out;

  not not_1 (not_1_out, Op[1]);
  not not_2 (not_2_out, Op[1]);
  not not_3 (not_3_out, Instr[3]);
  not not_4 (not_4_out, Instr[0]);
  not not_5 (not_5_out, Instr[3]);
  not not_6 (not_6_out, Op[0]);
  nor nor_1 (J, Op[0], not_1_out, Op[2], Op[3], Op[4], Op[5]);
  nor nor_2 (JAL, not_6_out, not_2_out, Op[2], Op[3], Op[4], Op[5]);
  nor nor_3 (nor_3_out, Op[0], Op[1], Op[2], Op[3], Op[4], Op[5]);
  nor nor_4 (nor_4_out, Instr[5], Instr[4], not_3_out, Instr[2], Instr[1], not_4_out);
  nor nor_5 (nor_5_out, Instr[5], Instr[4], not_5_out, Instr[2], Instr[1], Instr[0]);
  and and_1 (LinkReg, nor_3_out, nor_4_out);
  and and_2 (JR_t, nor_3_out, nor_5_out);
  or or_1 (Jump, J, JAL, LinkReg, JR_t);
  or or_2 (JR, LinkReg, JR_t);
  or or_3 (Link, JAL, LinkReg);

  // Other names for the same wires on the sheet: JALR = LinkReg
endmodule

module EpcCause (
  input  [31:0] CauseReg,
  input  [31:0] AdresaInstrukcije,
  input  Izuzetak,
  input  CLK,
  input  RST,
  output [31:0] CauseIzlaz,
  output [31:0] EpcIzlaz
);

  wire CLK_t;

  and and_1 (CLK_t, Izuzetak, CLK);
  Registar32bit Cause (.Ulaz(CauseReg), .CLK(CLK_t), .RST(RST), .Izlaz(CauseIzlaz));
  Registar32bit Epc (.Ulaz(AdresaInstrukcije), .CLK(CLK_t), .RST(RST), .Izlaz(EpcIzlaz));
endmodule

module MemSizeCheck (
  input  [31:0] Adress,
  input  MemRead,
  input  MemWrite,
  input  [4:0] Rs,
  output InvalidAdress
);

  wire eq5bit_1_izlaz, not_1_out, or_1_out, or_2_out;

  or or_1 (or_1_out, MemRead, MemWrite);
  or or_2 (or_2_out, Adress[25], Adress[26], Adress[27], Adress[28], Adress[29], Adress[30], Adress[31]);
  EQ5bit eq5bit_1 (.A(Rs), .B(5'b11101), .Izlaz(eq5bit_1_izlaz));
  not not_1 (not_1_out, eq5bit_1_izlaz);
  and and_1 (InvalidAdress, or_2_out, or_1_out, not_1_out);
endmodule

module ExceptionControl (
  input  Overflow,
  input  InvalidAdress,
  input  InvalidInsruction,
  output Exception,
  output [31:0] Cause
);

  wire not_1_out, not_2_out;

  not not_1 (not_1_out, InvalidAdress);
  not not_2 (not_2_out, InvalidInsruction);
  or or_1 (Exception, Overflow, InvalidAdress, InvalidInsruction);
  and and_1 (Cause[3], Overflow, not_1_out, not_2_out);
  and and_2 (Cause[2], InvalidAdress, not_2_out);

  assign {Cause[31:4], Cause[1:0]} = {30{1'b0}};
endmodule
